// Logisim project comparch.circ as structural Verilog: 8 circuits, main circuit four_bit_register
module four_bit_register (
  input  [3:0] in_1,
  output [3:0] out_2
);

  wire clock_1_out;

  Clock clock_1 (.out(clock_1_out));
  Register #(.width(4)) register_1 (.D(in_1), .en(1'b1), .clk(clock_1_out), .Q(out_2));  // open: clr
endmodule

module Ripple_carry_adder (
  input  [3:0] A,
  input  [3:0] B,
  input  C_in,
  output overflow,
  output [3:0] Output
);

  wire adder_2_cout, adder_3_cout, adder_4_cout;

  Adder #(.width(1)) adder_1 (.a(A[3]), .b(B[3]), .out(Output[3]), .cin(adder_2_cout), .cout(overflow));
  Adder #(.width(1)) adder_2 (.a(A[2]), .b(B[2]), .out(Output[2]), .cin(adder_3_cout), .cout(adder_2_cout));
  Adder #(.width(1)) adder_3 (.a(A[1]), .b(B[1]), .out(Output[1]), .cin(adder_4_cout), .cout(adder_3_cout));
  Adder #(.width(1)) adder_4 (.a(A[0]), .b(B[0]), .out(Output[0]), .cin(C_in), .cout(adder_4_cout));

  // Notes on the sheet:
  //   MSB
  //   LSB
endmodule

module ALU (
  input  WRITEorLOAD,
  input  [4:0] RegisterSelect_ALLSet,
  input  [31:0] Bit_Selection_BITWISE,
  input  EN_FOR_ALL,
  input  [31:0] ORIGINAL_INPUT,
  input  EN_FOR_WRITE_BITWISE,
  input  [4:0] Register_Select_WRITE_BITWISE,
  input  [4:0] Register_Select_READ1,
  input  [4:0] Register_Select_READ2,
  input  ext_SUB,
  input  [2:0] in_11,
  input  [1:0] in_12,
  output [31:0] REG1,
  output [31:0] REG2,
  output [31:0] ALUcomputedRESULT,
  output Zero_Flag,
  output Negative_Flag,
  output [31:0] ALU_OUTPUT,
  output out_19,
  output overflow,
  output [31:0] out_21
);

  wire adder_1_cout, adder_2_cout, adder_3_cout, adder_4_cout, adder_5_cout, adder_6_cout, adder_7_cout,
       adder_8_cout, adder_9_cout, adder_10_cout, adder_11_cout, adder_12_cout, adder_13_cout, adder_14_cout,
       adder_15_cout, adder_16_cout, adder_17_cout, adder_18_cout, adder_19_cout, adder_21_cout,
       adder_22_cout, adder_23_cout, adder_24_cout, adder_25_cout, adder_26_cout, adder_27_cout,
       adder_28_cout, adder_29_cout, adder_30_cout, adder_31_cout, adder_32_cout, and_2_out, and_3_out,
       and_4_out, clk_out, demultiplexer_1_out0, demultiplexer_1_out1, demultiplexer_1_out2,
       demultiplexer_1_out3, demultiplexer_1_out4, demultiplexer_1_out5, demultiplexer_1_out6,
       demultiplexer_1_out7, demultiplexer_1_out8, demultiplexer_1_out9, demultiplexer_1_out10,
       demultiplexer_1_out11, demultiplexer_1_out12, demultiplexer_1_out13, demultiplexer_1_out14,
       demultiplexer_1_out15, demultiplexer_1_out16, demultiplexer_1_out17, demultiplexer_1_out18,
       demultiplexer_1_out19, demultiplexer_1_out20, demultiplexer_1_out21, demultiplexer_1_out22,
       demultiplexer_1_out23, demultiplexer_1_out24, demultiplexer_1_out25, demultiplexer_1_out26,
       demultiplexer_1_out27, demultiplexer_1_out28, demultiplexer_1_out29, demultiplexer_1_out30,
       demultiplexer_1_out31, or_2_out, or_3_out, or_4_out, xor_10_out;
  wire [0:0] not_2_out, xor_11_out;
  wire [3:0] xor_2_out, xor_3_out, xor_4_out, xor_5_out, xor_6_out, xor_7_out, xor_8_out, xor_9_out;
  wire [3:3] or_5_out;
  wire [31:0] and_1_out, multiplexer_1_out, multiplexer_3_out, multiplexer_4_out, multiplexer_5_out,
       multiplexer_6_out, multiplexer_7_out, multiplexer_8_out, multiplexer_9_out, multiplexer_10_out,
       multiplexer_11_out, multiplexer_12_out, multiplexer_13_out, multiplexer_14_out, multiplexer_15_out,
       multiplexer_16_out, multiplexer_17_out, multiplexer_18_out, or_1_out, undriven, xor_1_out;

  assign and_1_out = REG1 & REG2;  // AND_Gate and_1, 32 bits wide
  assign or_1_out = REG1 | REG2;  // OR_Gate or_1, 32 bits wide
  assign xor_1_out = REG1 ^ REG2;  // XOR_Gate xor_1, 32 bits wide
  Adder #(.width(1)) adder_1 (.a(REG1[3]), .b(xor_2_out[3]), .out(out_21[3]), .cin(adder_5_cout), .cout(adder_1_cout));
  Adder #(.width(1)) adder_2 (.a(REG1[7]), .b(xor_3_out[3]), .out(out_21[7]), .cin(adder_6_cout), .cout(adder_2_cout));
  Adder #(.width(1)) adder_3 (
    .a(REG1[11]), .b(xor_4_out[3]), .out(out_21[11]), .cin(adder_7_cout), .cout(adder_3_cout));
  Adder #(.width(1)) adder_4 (
    .a(REG1[15]), .b(xor_5_out[3]), .out(out_21[15]), .cin(adder_8_cout), .cout(adder_4_cout));
  Demultiplexer #(.select(5)) demultiplexer_1 (
    .out0(demultiplexer_1_out0), .out1(demultiplexer_1_out1), .out2(demultiplexer_1_out2),
    .out3(demultiplexer_1_out3), .out4(demultiplexer_1_out4), .out5(demultiplexer_1_out5),
    .out6(demultiplexer_1_out6), .out7(demultiplexer_1_out7), .out8(demultiplexer_1_out8),
    .out9(demultiplexer_1_out9), .out10(demultiplexer_1_out10), .out11(demultiplexer_1_out11),
    .out12(demultiplexer_1_out12), .out13(demultiplexer_1_out13), .out14(demultiplexer_1_out14),
    .out15(demultiplexer_1_out15), .out16(demultiplexer_1_out16), .out17(demultiplexer_1_out17),
    .out18(demultiplexer_1_out18), .out19(demultiplexer_1_out19), .out20(demultiplexer_1_out20),
    .out21(demultiplexer_1_out21), .out22(demultiplexer_1_out22), .out23(demultiplexer_1_out23),
    .out24(demultiplexer_1_out24), .out25(demultiplexer_1_out25), .out26(demultiplexer_1_out26),
    .out27(demultiplexer_1_out27), .out28(demultiplexer_1_out28), .out29(demultiplexer_1_out29),
    .out30(demultiplexer_1_out30), .out31(demultiplexer_1_out31), .in(EN_FOR_WRITE_BITWISE),
    .sel(Register_Select_WRITE_BITWISE));
  Adder #(.width(1)) adder_5 (.a(REG1[2]), .b(xor_2_out[2]), .out(out_21[2]), .cin(adder_9_cout), .cout(adder_5_cout));
  Adder #(.width(1)) adder_6 (.a(REG1[6]), .b(xor_3_out[2]), .out(out_21[6]), .cin(adder_10_cout), .cout(adder_6_cout));
  Adder #(.width(1)) adder_7 (
    .a(REG1[10]), .b(xor_4_out[2]), .out(out_21[10]), .cin(adder_11_cout), .cout(adder_7_cout));
  Adder #(.width(1)) adder_8 (
    .a(REG1[14]), .b(xor_5_out[2]), .out(out_21[14]), .cin(adder_12_cout), .cout(adder_8_cout));
  Multiplexer #(.width(32)) multiplexer_1 (
    .in0(ORIGINAL_INPUT), .in1(ALUcomputedRESULT), .out(multiplexer_1_out), .sel(WRITEorLOAD));
  assign xor_2_out = REG2[3:0] ^ {4{or_5_out[3]}};  // XOR_Gate xor_2, 4 bits wide
  Adder #(.width(1)) adder_9 (.a(REG1[1]), .b(xor_2_out[1]), .out(out_21[1]), .cin(adder_13_cout), .cout(adder_9_cout));
  assign xor_3_out = REG2[7:4] ^ {4{or_5_out[3]}};  // XOR_Gate xor_3, 4 bits wide
  assign xor_4_out = REG2[11:8] ^ {4{or_5_out[3]}};  // XOR_Gate xor_4, 4 bits wide
  assign xor_5_out = REG2[15:12] ^ {4{or_5_out[3]}};  // XOR_Gate xor_5, 4 bits wide
  not not_1 (Zero_Flag, or_2_out);
  Adder #(.width(1)) adder_10 (
    .a(REG1[5]), .b(xor_3_out[1]), .out(out_21[5]), .cin(adder_14_cout), .cout(adder_10_cout));
  Adder #(.width(1)) adder_11 (
    .a(REG1[9]), .b(xor_4_out[1]), .out(out_21[9]), .cin(adder_15_cout), .cout(adder_11_cout));
  Adder #(.width(1)) adder_12 (
    .a(REG1[13]), .b(xor_5_out[1]), .out(out_21[13]), .cin(adder_16_cout), .cout(adder_12_cout));
  or or_2 (or_2_out, out_21[5], out_21[0], out_21[1], out_21[2], out_21[3], out_21[4], out_21[6], out_21[7], out_21[8], out_21[9], out_21[10], out_21[11], out_21[12], out_21[13], out_21[14], out_21[15], out_21[16], out_21[17], out_21[18], out_21[19], out_21[20], out_21[21], out_21[22], out_21[23], out_21[24], out_21[25], out_21[26], out_21[27], out_21[28], out_21[29], out_21[30], Negative_Flag);
  Adder #(.width(1)) adder_13 (.a(REG1[0]), .b(xor_2_out[0]), .out(out_21[0]), .cin(or_5_out[3]), .cout(adder_13_cout));
  Adder #(.width(1)) adder_14 (
    .a(REG1[4]), .b(xor_3_out[0]), .out(out_21[4]), .cin(adder_1_cout), .cout(adder_14_cout));
  Adder #(.width(1)) adder_15 (
    .a(REG1[8]), .b(xor_4_out[0]), .out(out_21[8]), .cin(adder_2_cout), .cout(adder_15_cout));
  Adder #(.width(1)) adder_16 (
    .a(REG1[12]), .b(xor_5_out[0]), .out(out_21[12]), .cin(adder_3_cout), .cout(adder_16_cout));
  Clock clk (.out(clk_out));
  assign xor_6_out = REG2[31:28] ^ {4{or_5_out[3]}};  // XOR_Gate xor_6, 4 bits wide
  Adder #(.width(1)) adder_17 (
    .a(REG1[19]), .b(xor_9_out[3]), .out(out_21[19]), .cin(adder_21_cout), .cout(adder_17_cout));
  Multiplexer #(.select(3), .width(32)) multiplexer_2 (
    .in0({Negative_Flag, out_21[30:0]}), .in1({Negative_Flag, out_21[30:0]}), .in2(and_1_out),
    .in3(or_1_out), .in4(xor_1_out), .in5({{31{1'b0}}, xor_11_out[0]}), .in6({{31{1'b0}}, not_2_out[0]}),
    .in7(multiplexer_18_out), .out(ALU_OUTPUT), .sel(in_11));
  assign xor_7_out = REG2[27:24] ^ {4{or_5_out[3]}};  // XOR_Gate xor_7, 4 bits wide
  Adder #(.width(1)) adder_18 (
    .a(REG1[23]), .b(xor_8_out[3]), .out(out_21[23]), .cin(adder_22_cout), .cout(adder_18_cout));
  Adder #(.width(1)) adder_19 (
    .a(REG1[27]), .b(xor_7_out[3]), .out(out_21[27]), .cin(adder_23_cout), .cout(adder_19_cout));
  Adder #(.width(1)) adder_20 (.a(REG1[31]), .b(xor_6_out[3]), .out(Negative_Flag), .cin(adder_24_cout), .cout(out_19));
  assign xor_8_out = REG2[23:20] ^ {4{or_5_out[3]}};  // XOR_Gate xor_8, 4 bits wide
  Adder #(.width(1)) adder_21 (
    .a(REG1[18]), .b(xor_9_out[2]), .out(out_21[18]), .cin(adder_25_cout), .cout(adder_21_cout));
  Adder #(.width(1)) adder_22 (
    .a(REG1[22]), .b(xor_8_out[2]), .out(out_21[22]), .cin(adder_26_cout), .cout(adder_22_cout));
  Adder #(.width(1)) adder_23 (
    .a(REG1[26]), .b(xor_7_out[2]), .out(out_21[26]), .cin(adder_27_cout), .cout(adder_23_cout));
  Adder #(.width(1)) adder_24 (
    .a(REG1[30]), .b(xor_6_out[2]), .out(out_21[30]), .cin(adder_28_cout), .cout(adder_24_cout));
  assign xor_9_out = REG2[19:16] ^ {4{or_5_out[3]}};  // XOR_Gate xor_9, 4 bits wide
  Adder #(.width(1)) adder_25 (
    .a(REG1[17]), .b(xor_9_out[1]), .out(out_21[17]), .cin(adder_29_cout), .cout(adder_25_cout));
  copypasteregisterfile RegisterFile (
    .BitPicking(Bit_Selection_BITWISE), .DECODER_INPUT_ADDRESSING_AllSets(RegisterSelect_ALLSet),
    .Main_INPUT(multiplexer_1_out), .ENforALLSet(EN_FOR_ALL), .R0Selection(demultiplexer_1_out0),
    .CLK(clk_out), .R1Selection(demultiplexer_1_out1), .R2Selection(demultiplexer_1_out2),
    .R16Selection(demultiplexer_1_out16), .R3Selection(demultiplexer_1_out3),
    .R17Selection(demultiplexer_1_out17), .R18Selection(demultiplexer_1_out18),
    .READ1_SELECT(Register_Select_READ1), .R19Selection(demultiplexer_1_out19),
    .R4Selection(demultiplexer_1_out4), .R5Selection(demultiplexer_1_out5),
    .R20Selection(demultiplexer_1_out20), .R6Selection(demultiplexer_1_out6),
    .R21Selection(demultiplexer_1_out21), .R7Selection(demultiplexer_1_out7),
    .R22Selection(demultiplexer_1_out22), .READ2_SELECT(Register_Select_READ2),
    .R23Selection(demultiplexer_1_out23), .R8Selection(demultiplexer_1_out8),
    .R9Selection(demultiplexer_1_out9), .R24Selection(demultiplexer_1_out24),
    .R10Selection(demultiplexer_1_out10), .R25Selection(demultiplexer_1_out25),
    .R11Selection(demultiplexer_1_out11), .R26Selection(demultiplexer_1_out26),
    .R27Selection(demultiplexer_1_out27), .R12Selection(demultiplexer_1_out12),
    .R13Selection(demultiplexer_1_out13), .R28Selection(demultiplexer_1_out28),
    .R14Selection(demultiplexer_1_out14), .R29Selection(demultiplexer_1_out29),
    .R15Selection(demultiplexer_1_out15), .R30Selection(demultiplexer_1_out30),
    .R31Selection(demultiplexer_1_out31), .READ1_OUTPUT(REG1), .READ2_OUTPUT(REG2));
  and and_2 (and_2_out, ~in_11[2], ~in_11[1], in_11[0]);  // AND_Gate
  and and_3 (and_3_out, in_11[0], ~in_11[1], in_11[2]);  // AND_Gate
  and and_4 (and_4_out, ~in_11[0], in_11[1], in_11[2]);  // AND_Gate
  Adder #(.width(1)) adder_26 (
    .a(REG1[21]), .b(xor_8_out[1]), .out(out_21[21]), .cin(adder_30_cout), .cout(adder_26_cout));
  Adder #(.width(1)) adder_27 (
    .a(REG1[25]), .b(xor_7_out[1]), .out(out_21[25]), .cin(adder_31_cout), .cout(adder_27_cout));
  Adder #(.width(1)) adder_28 (
    .a(REG1[29]), .b(xor_6_out[1]), .out(out_21[29]), .cin(adder_32_cout), .cout(adder_28_cout));
  xor xor_10 (xor_10_out, adder_19_cout, out_19);
  xor xor_11 (xor_11_out[0], xor_10_out, Negative_Flag);
  not not_2 (not_2_out[0], out_19);
  or or_3 (or_3_out, ext_SUB, and_3_out);
  or or_4 (or_4_out, ext_SUB, and_4_out);
  Adder #(.width(1)) adder_29 (
    .a(REG1[16]), .b(xor_9_out[0]), .out(out_21[16]), .cin(adder_4_cout), .cout(adder_29_cout));
  Adder #(.width(1)) adder_30 (
    .a(REG1[20]), .b(xor_8_out[0]), .out(out_21[20]), .cin(adder_17_cout), .cout(adder_30_cout));
  Adder #(.width(1)) adder_31 (
    .a(REG1[24]), .b(xor_7_out[0]), .out(out_21[24]), .cin(adder_18_cout), .cout(adder_31_cout));
  Adder #(.width(1)) adder_32 (
    .a(REG1[28]), .b(xor_6_out[0]), .out(out_21[28]), .cin(adder_19_cout), .cout(adder_32_cout));
  or or_5 (or_5_out[3], or_3_out, and_2_out, or_4_out);
  Multiplexer #(.width(32)) multiplexer_3 (
    .in0(REG1), .in1({REG1[30:0], 1'b0}), .out(multiplexer_3_out), .sel(REG2[0]));
  Multiplexer #(.width(32)) multiplexer_4 (
    .in0(REG1), .in1({1'b0, REG1[31:1]}), .out(multiplexer_4_out), .sel(REG2[0]));
  Multiplexer #(.width(32)) multiplexer_5 (
    .in0(REG1), .in1({{2{REG1[31]}}, REG1[30:1]}), .out(multiplexer_5_out), .sel(REG2[0]));
  Register32Bit ALUspecialregister (
    .EN0(EN_FOR_ALL), .EN1(EN_FOR_ALL), .clk(clk_out), .EN2(EN_FOR_ALL), .EN3(EN_FOR_ALL),
    .InputData(ALU_OUTPUT), .EN16(EN_FOR_ALL), .EN17(EN_FOR_ALL), .EN4(EN_FOR_ALL), .EN5(EN_FOR_ALL),
    .EN6(EN_FOR_ALL), .EN7(EN_FOR_ALL), .EN18(EN_FOR_ALL), .EN19(EN_FOR_ALL), .EN8(EN_FOR_ALL),
    .EN9(EN_FOR_ALL), .EN20(EN_FOR_ALL), .EN21(EN_FOR_ALL), .EN10(EN_FOR_ALL), .EN11(EN_FOR_ALL),
    .EN22(EN_FOR_ALL), .EN23(EN_FOR_ALL), .EN12(EN_FOR_ALL), .EN13(EN_FOR_ALL), .EN24(EN_FOR_ALL),
    .EN25(EN_FOR_ALL), .EN14(EN_FOR_ALL), .EN15(EN_FOR_ALL), .EN26(EN_FOR_ALL), .EN27(EN_FOR_ALL),
    .EN28(EN_FOR_ALL), .EN29(EN_FOR_ALL), .EN30(EN_FOR_ALL), .EN31(EN_FOR_ALL), .OutputData(ALUcomputedRESULT));
  Multiplexer #(.width(32)) multiplexer_6 (
    .in0(multiplexer_3_out), .in1({multiplexer_3_out[29:0], 2'b00}), .out(multiplexer_6_out), .sel(REG2[1]));
  Multiplexer #(.width(32)) multiplexer_7 (
    .in0(multiplexer_4_out), .in1({2'b00, multiplexer_4_out[31:2]}), .out(multiplexer_7_out), .sel(REG2[1]));
  Multiplexer #(.width(32)) multiplexer_8 (
    .in0(multiplexer_5_out), .in1({{3{multiplexer_5_out[31]}}, multiplexer_5_out[30:2]}),
    .out(multiplexer_8_out), .sel(REG2[1]));
  Multiplexer #(.width(32)) multiplexer_9 (
    .in0(multiplexer_6_out), .in1({multiplexer_6_out[27:0], 4'b0000}), .out(multiplexer_9_out), .sel(REG2[2]));
  Multiplexer #(.width(32)) multiplexer_10 (
    .in0(multiplexer_7_out), .in1({4'b0000, multiplexer_7_out[31:4]}), .out(multiplexer_10_out), .sel(REG2[2]));
  Multiplexer #(.width(32)) multiplexer_11 (
    .in0(multiplexer_8_out), .in1({{5{multiplexer_8_out[31]}}, multiplexer_8_out[30:4]}),
    .out(multiplexer_11_out), .sel(REG2[2]));
  Multiplexer #(.width(32)) multiplexer_12 (
    .in0(multiplexer_9_out), .in1({multiplexer_9_out[23:0], {8{1'b0}}}), .out(multiplexer_12_out),
    .sel(REG2[3]));
  Multiplexer #(.width(32)) multiplexer_13 (
    .in0(multiplexer_10_out), .in1({{8{1'b0}}, multiplexer_10_out[31:8]}), .out(multiplexer_13_out),
    .sel(REG2[3]));
  Multiplexer #(.width(32)) multiplexer_14 (
    .in0(multiplexer_11_out), .in1({{9{multiplexer_11_out[31]}}, multiplexer_11_out[30:8]}),
    .out(multiplexer_14_out), .sel(REG2[3]));
  Multiplexer #(.width(32)) multiplexer_15 (
    .in0(multiplexer_12_out), .in1({multiplexer_12_out[15:0], {16{1'b0}}}), .out(multiplexer_15_out),
    .sel(REG2[4]));
  Multiplexer #(.width(32)) multiplexer_16 (
    .in0(multiplexer_13_out), .in1({{15{1'b0}}, multiplexer_13_out[31:15]}), .out(multiplexer_16_out),
    .sel(REG2[4]));
  Multiplexer #(.width(32)) multiplexer_17 (
    .in0(multiplexer_14_out), .in1(undriven), .out(multiplexer_17_out), .sel(REG2[4]));
  Multiplexer #(.select(2), .width(32)) multiplexer_18 (
    .in0(multiplexer_15_out), .in1(multiplexer_16_out), .in2(multiplexer_17_out), .out(multiplexer_18_out),
    .sel(in_12));  // open: in3

  assign out_21[31] = Negative_Flag;
  assign overflow = out_19;

  // Notes on the sheet:
  //   Output
  //   Output
  //   SLICE O
  //   SLICE 1
  //   SLICE 2
  //   SLICE 3
  //   000 ADD
  //   001 SUB
  //   010 AND
  //   011 OR
  //   100 X-OR
  //   101 SLT
  //   110 SLTU
  //   111 SHIFT
  //   Output
  //   Output
  //   Output
  //   Carry_Out/Overflow Flag
  //   SLICE 4
  //   SLICE 5
  //   SLICE 6
  //   SLICE 7
  //   int_SUB
  //   Signed SLT bit
  //   Shift by 1 Bit
  //   Shift by 1 Bit
  //   Shift by 1 Bit
  //   Shift by 2 Bit
  //   Shift by 2 Bit
  //   Shift by 2 Bit
  //   Shift by 4 Bit
  //   Shift by 4 Bit
  //   Shift by 4 Bit
  //   Shift by 8 Bit
  //   Shift by 8 Bit
  //   Shift by 8 Bit
  //   Shift by 16 Bit
  //   Shift by 16 Bit
  //   Shift by 16 Bit
  //   Input For SLL, SRL, SRA
endmodule

module Register32Bit (
  input  EN0,
  input  EN1,
  input  clk,
  input  EN2,
  input  EN3,
  input  [31:0] InputData,
  input  EN16,
  input  EN17,
  input  EN4,
  input  EN5,
  input  EN6,
  input  EN7,
  input  EN18,
  input  EN19,
  input  EN8,
  input  EN9,
  input  EN20,
  input  EN21,
  input  EN10,
  input  EN11,
  input  EN22,
  input  EN23,
  input  EN12,
  input  EN13,
  input  EN24,
  input  EN25,
  input  EN14,
  input  EN15,
  input  EN26,
  input  EN27,
  input  EN28,
  input  EN29,
  input  EN30,
  input  EN31,
  output [31:0] OutputData
);

  wire multiplexer_1_out, multiplexer_2_out, multiplexer_3_out, multiplexer_4_out, multiplexer_5_out,
       multiplexer_6_out, multiplexer_7_out, multiplexer_8_out, multiplexer_9_out, multiplexer_10_out,
       multiplexer_11_out, multiplexer_12_out, multiplexer_13_out, multiplexer_14_out, multiplexer_15_out,
       multiplexer_16_out, multiplexer_17_out, multiplexer_18_out, multiplexer_19_out, multiplexer_20_out,
       multiplexer_21_out, multiplexer_22_out, multiplexer_23_out, multiplexer_24_out, multiplexer_25_out,
       multiplexer_26_out, multiplexer_27_out, multiplexer_28_out, multiplexer_29_out, multiplexer_30_out,
       multiplexer_31_out, multiplexer_32_out;

  Multiplexer multiplexer_1 (.in0(OutputData[0]), .in1(InputData[0]), .out(multiplexer_1_out), .sel(EN0));
  Multiplexer multiplexer_2 (.in0(OutputData[2]), .in1(InputData[2]), .out(multiplexer_2_out), .sel(EN2));
  Multiplexer multiplexer_3 (.in0(OutputData[4]), .in1(InputData[4]), .out(multiplexer_3_out), .sel(EN4));
  Multiplexer multiplexer_4 (.in0(OutputData[6]), .in1(InputData[6]), .out(multiplexer_4_out), .sel(EN6));
  Multiplexer multiplexer_5 (.in0(OutputData[8]), .in1(InputData[8]), .out(multiplexer_5_out), .sel(EN8));
  Multiplexer multiplexer_6 (.in0(OutputData[10]), .in1(InputData[10]), .out(multiplexer_6_out), .sel(EN10));
  Multiplexer multiplexer_7 (.in0(OutputData[12]), .in1(InputData[12]), .out(multiplexer_7_out), .sel(EN12));
  Multiplexer multiplexer_8 (.in0(OutputData[14]), .in1(InputData[14]), .out(multiplexer_8_out), .sel(EN14));
  D_Flip_Flop d_ff_1 (.D(multiplexer_1_out), .clk(clk), .Q(OutputData[0]), .preset(1'b0), .reset(1'b0));  // open: Qn
  D_Flip_Flop d_ff_2 (.D(multiplexer_2_out), .clk(clk), .Q(OutputData[2]), .preset(1'b0), .reset(1'b0));  // open: Qn
  D_Flip_Flop d_ff_3 (.D(multiplexer_3_out), .clk(clk), .Q(OutputData[4]), .preset(1'b0), .reset(1'b0));  // open: Qn
  D_Flip_Flop d_ff_4 (.D(multiplexer_4_out), .clk(clk), .Q(OutputData[6]), .preset(1'b0), .reset(1'b0));  // open: Qn
  D_Flip_Flop d_ff_5 (.D(multiplexer_5_out), .clk(clk), .Q(OutputData[8]), .preset(1'b0), .reset(1'b0));  // open: Qn
  D_Flip_Flop d_ff_6 (.D(multiplexer_6_out), .clk(clk), .Q(OutputData[10]), .preset(1'b0), .reset(1'b0));  // open: Qn
  D_Flip_Flop d_ff_7 (.D(multiplexer_7_out), .clk(clk), .Q(OutputData[12]), .preset(1'b0), .reset(1'b0));  // open: Qn
  D_Flip_Flop d_ff_8 (.D(multiplexer_8_out), .clk(clk), .Q(OutputData[14]), .preset(1'b0), .reset(1'b0));  // open: Qn
  Multiplexer multiplexer_9 (.in0(OutputData[1]), .in1(InputData[1]), .out(multiplexer_9_out), .sel(EN1));
  Multiplexer multiplexer_10 (.in0(OutputData[3]), .in1(InputData[3]), .out(multiplexer_10_out), .sel(EN3));
  Multiplexer multiplexer_11 (.in0(OutputData[5]), .in1(InputData[5]), .out(multiplexer_11_out), .sel(EN5));
  Multiplexer multiplexer_12 (.in0(OutputData[7]), .in1(InputData[7]), .out(multiplexer_12_out), .sel(EN7));
  Multiplexer multiplexer_13 (.in0(OutputData[9]), .in1(InputData[9]), .out(multiplexer_13_out), .sel(EN9));
  Multiplexer multiplexer_14 (.in0(OutputData[11]), .in1(InputData[11]), .out(multiplexer_14_out), .sel(EN11));
  Multiplexer multiplexer_15 (.in0(OutputData[13]), .in1(InputData[13]), .out(multiplexer_15_out), .sel(EN13));
  Multiplexer multiplexer_16 (.in0(OutputData[15]), .in1(InputData[15]), .out(multiplexer_16_out), .sel(EN15));
  D_Flip_Flop d_ff_9 (.D(multiplexer_9_out), .clk(clk), .Q(OutputData[1]), .preset(1'b0), .reset(1'b0));  // open: Qn
  D_Flip_Flop d_ff_10 (.D(multiplexer_10_out), .clk(clk), .Q(OutputData[3]), .preset(1'b0), .reset(1'b0));  // open: Qn
  D_Flip_Flop d_ff_11 (.D(multiplexer_11_out), .clk(clk), .Q(OutputData[5]), .preset(1'b0), .reset(1'b0));  // open: Qn
  D_Flip_Flop d_ff_12 (.D(multiplexer_12_out), .clk(clk), .Q(OutputData[7]), .preset(1'b0), .reset(1'b0));  // open: Qn
  D_Flip_Flop d_ff_13 (.D(multiplexer_13_out), .clk(clk), .Q(OutputData[9]), .preset(1'b0), .reset(1'b0));  // open: Qn
  D_Flip_Flop d_ff_14 (.D(multiplexer_14_out), .clk(clk), .Q(OutputData[11]), .preset(1'b0), .reset(1'b0));  // open: Qn
  D_Flip_Flop d_ff_15 (.D(multiplexer_15_out), .clk(clk), .Q(OutputData[13]), .preset(1'b0), .reset(1'b0));  // open: Qn
  D_Flip_Flop d_ff_16 (.D(multiplexer_16_out), .clk(clk), .Q(OutputData[15]), .preset(1'b0), .reset(1'b0));  // open: Qn
  Multiplexer multiplexer_17 (.in0(OutputData[16]), .in1(InputData[16]), .out(multiplexer_17_out), .sel(EN16));
  Multiplexer multiplexer_18 (.in0(OutputData[18]), .in1(InputData[18]), .out(multiplexer_18_out), .sel(EN18));
  Multiplexer multiplexer_19 (.in0(OutputData[20]), .in1(InputData[20]), .out(multiplexer_19_out), .sel(EN20));
  Multiplexer multiplexer_20 (.in0(OutputData[22]), .in1(InputData[22]), .out(multiplexer_20_out), .sel(EN22));
  Multiplexer multiplexer_21 (.in0(OutputData[24]), .in1(InputData[24]), .out(multiplexer_21_out), .sel(EN24));
  Multiplexer multiplexer_22 (.in0(OutputData[26]), .in1(InputData[26]), .out(multiplexer_22_out), .sel(EN26));
  Multiplexer multiplexer_23 (.in0(OutputData[28]), .in1(InputData[28]), .out(multiplexer_23_out), .sel(EN28));
  Multiplexer multiplexer_24 (.in0(OutputData[30]), .in1(InputData[30]), .out(multiplexer_24_out), .sel(EN30));
  D_Flip_Flop d_ff_17 (.D(multiplexer_17_out), .clk(clk), .Q(OutputData[16]), .preset(1'b0), .reset(1'b0));  // open: Qn
  D_Flip_Flop d_ff_18 (.D(multiplexer_18_out), .clk(clk), .Q(OutputData[18]), .preset(1'b0), .reset(1'b0));  // open: Qn
  D_Flip_Flop d_ff_19 (.D(multiplexer_19_out), .clk(clk), .Q(OutputData[20]), .preset(1'b0), .reset(1'b0));  // open: Qn
  D_Flip_Flop d_ff_20 (.D(multiplexer_20_out), .clk(clk), .Q(OutputData[22]), .preset(1'b0), .reset(1'b0));  // open: Qn
  D_Flip_Flop d_ff_21 (.D(multiplexer_21_out), .clk(clk), .Q(OutputData[24]), .preset(1'b0), .reset(1'b0));  // open: Qn
  D_Flip_Flop d_ff_22 (.D(multiplexer_22_out), .clk(clk), .Q(OutputData[26]), .preset(1'b0), .reset(1'b0));  // open: Qn
  D_Flip_Flop d_ff_23 (.D(multiplexer_23_out), .clk(clk), .Q(OutputData[28]), .preset(1'b0), .reset(1'b0));  // open: Qn
  D_Flip_Flop d_ff_24 (.D(multiplexer_24_out), .clk(clk), .Q(OutputData[30]), .preset(1'b0), .reset(1'b0));  // open: Qn
  Multiplexer multiplexer_25 (.in0(OutputData[17]), .in1(InputData[17]), .out(multiplexer_25_out), .sel(EN17));
  Multiplexer multiplexer_26 (.in0(OutputData[19]), .in1(InputData[19]), .out(multiplexer_26_out), .sel(EN19));
  Multiplexer multiplexer_27 (.in0(OutputData[21]), .in1(InputData[21]), .out(multiplexer_27_out), .sel(EN21));
  Multiplexer multiplexer_28 (.in0(OutputData[23]), .in1(InputData[23]), .out(multiplexer_28_out), .sel(EN23));
  Multiplexer multiplexer_29 (.in0(OutputData[25]), .in1(InputData[25]), .out(multiplexer_29_out), .sel(EN25));
  Multiplexer multiplexer_30 (.in0(OutputData[27]), .in1(InputData[27]), .out(multiplexer_30_out), .sel(EN27));
  Multiplexer multiplexer_31 (.in0(OutputData[29]), .in1(InputData[29]), .out(multiplexer_31_out), .sel(EN29));
  Multiplexer multiplexer_32 (.in0(OutputData[31]), .in1(InputData[31]), .out(multiplexer_32_out), .sel(EN31));
  D_Flip_Flop d_ff_25 (.D(multiplexer_25_out), .clk(clk), .Q(OutputData[17]), .preset(1'b0), .reset(1'b0));  // open: Qn
  D_Flip_Flop d_ff_26 (.D(multiplexer_26_out), .clk(clk), .Q(OutputData[19]), .preset(1'b0), .reset(1'b0));  // open: Qn
  D_Flip_Flop d_ff_27 (.D(multiplexer_27_out), .clk(clk), .Q(OutputData[21]), .preset(1'b0), .reset(1'b0));  // open: Qn
  D_Flip_Flop d_ff_28 (.D(multiplexer_28_out), .clk(clk), .Q(OutputData[23]), .preset(1'b0), .reset(1'b0));  // open: Qn
  D_Flip_Flop d_ff_29 (.D(multiplexer_29_out), .clk(clk), .Q(OutputData[25]), .preset(1'b0), .reset(1'b0));  // open: Qn
  D_Flip_Flop d_ff_30 (.D(multiplexer_30_out), .clk(clk), .Q(OutputData[27]), .preset(1'b0), .reset(1'b0));  // open: Qn
  D_Flip_Flop d_ff_31 (.D(multiplexer_31_out), .clk(clk), .Q(OutputData[29]), .preset(1'b0), .reset(1'b0));  // open: Qn
  D_Flip_Flop d_ff_32 (.D(multiplexer_32_out), .clk(clk), .Q(OutputData[31]), .preset(1'b0), .reset(1'b0));  // open: Qn

  // Notes on the sheet:
  //   D_in
  //   D_in
  //   Enable
  //   Enable
  //   D_in
  //   D_in
  //   Enable
  //   Enable
  //   D_in
  //   D_in
  //   Enable
  //   Enable
  //   D_in
  //   Enable
  //   D_in
  //   Enable
endmodule

module RegisterFile (
  input  [31:0] in_1,
  input  [4:0] in_2,
  input  [31:0] in_3,
  input  in_4,
  input  in_5,
  input  in_6,
  input  in_7,
  input  in_8,
  input  in_9,
  input  in_10,
  input  in_11,
  input  in_12,
  input  in_13,
  input  in_14,
  input  in_15,
  input  in_16,
  input  in_17,
  input  in_18,
  input  in_19,
  input  in_20,
  input  in_21,
  input  in_22,
  input  in_23,
  input  in_24,
  input  in_25,
  input  in_26,
  input  in_27,
  input  in_28,
  input  in_29,
  input  in_30,
  input  in_31,
  input  in_32,
  input  in_33,
  input  in_34,
  input  in_35,
  input  in_36,
  output [31:0] out_37
);

  wire and_1_out, and_2_out, and_3_out, and_4_out, and_5_out, and_6_out, and_7_out, and_8_out, and_9_out,
       and_10_out, and_11_out, and_12_out, and_13_out, and_14_out, and_15_out, and_16_out, and_17_out,
       and_18_out, and_19_out, and_20_out, and_21_out, and_22_out, and_23_out, and_24_out, and_25_out,
       and_26_out, and_27_out, and_28_out, and_29_out, and_30_out, and_31_out, and_32_out, B00000_out,
       B00001_out, B00010_out, B00011_out, B00100_out, B00101_out, B00110_out, B00111_out, B01000_out,
       B01001_out, B01010_out, B01011_out, B01100_out, B01101_out, B01110_out, B01111_out, B10000_out,
       B10001_out, B10010_out, B10011_out, B10100_out, B10101_out, B10110_out, B10111_out, B11000_out,
       B11001_out, B11010_out, B11011_out, B11100_out, B11101_out, B11110_out, B11111_out, clock_1_out,
       not_1_out, not_2_out, not_3_out, not_4_out, not_5_out;
  wire [31:0] demultiplexer_1_out0, demultiplexer_1_out1, demultiplexer_1_out2, demultiplexer_1_out3,
       demultiplexer_1_out4, demultiplexer_1_out5, demultiplexer_1_out6, demultiplexer_1_out7,
       demultiplexer_1_out8, demultiplexer_1_out9, demultiplexer_1_out10, demultiplexer_1_out11,
       demultiplexer_1_out12, demultiplexer_1_out13, demultiplexer_1_out14, demultiplexer_1_out15,
       demultiplexer_1_out16, demultiplexer_1_out17, demultiplexer_1_out18, demultiplexer_1_out19,
       demultiplexer_1_out20, demultiplexer_1_out21, demultiplexer_1_out22, demultiplexer_1_out23,
       demultiplexer_1_out24, demultiplexer_1_out25, demultiplexer_1_out26, demultiplexer_1_out27,
       demultiplexer_1_out28, demultiplexer_1_out29, demultiplexer_1_out30, demultiplexer_1_out31,
       smallstuff_1_out_3, smallstuff_2_out_3, smallstuff_3_out_3, smallstuff_4_out_3, smallstuff_5_out_3,
       smallstuff_6_out_3, smallstuff_7_out_3, smallstuff_8_out_3, smallstuff_9_out_3, smallstuff_10_out_3,
       smallstuff_11_out_3, smallstuff_12_out_3, smallstuff_13_out_3, smallstuff_14_out_3,
       smallstuff_15_out_3, smallstuff_16_out_3, smallstuff_17_out_3, smallstuff_18_out_3,
       smallstuff_20_out_3, smallstuff_21_out_3, smallstuff_22_out_3, smallstuff_23_out_3,
       smallstuff_24_out_3, smallstuff_25_out_3, smallstuff_26_out_3, smallstuff_27_out_3,
       smallstuff_28_out_3, smallstuff_29_out_3, smallstuff_30_out_3, smallstuff_31_out_3,
       smallstuff_32_out_3;

  not not_1 (not_1_out, in_2[4]);
  not not_2 (not_2_out, in_2[3]);
  not not_3 (not_3_out, in_2[2]);
  not not_4 (not_4_out, in_2[1]);
  not not_5 (not_5_out, in_2[0]);
  and B00000 (B00000_out, not_5_out, not_4_out, not_3_out, not_2_out, not_1_out);
  and B00001 (B00001_out, in_2[0], not_4_out, not_3_out, not_2_out, not_1_out);
  and B00010 (B00010_out, not_5_out, in_2[1], not_3_out, not_2_out, not_1_out);
  and B00011 (B00011_out, in_2[0], in_2[1], not_3_out, not_2_out, not_1_out);
  and B00100 (B00100_out, not_5_out, not_4_out, in_2[2], not_2_out, not_1_out);
  and B00101 (B00101_out, in_2[0], not_4_out, in_2[2], not_2_out, not_1_out);
  and B00110 (B00110_out, not_5_out, in_2[1], in_2[2], not_2_out, not_1_out);
  and B00111 (B00111_out, in_2[0], in_2[1], in_2[2], not_2_out, not_1_out);
  and B01000 (B01000_out, not_5_out, not_4_out, not_3_out, in_2[3], not_1_out);
  and B01001 (B01001_out, in_2[0], not_4_out, not_3_out, in_2[3], not_1_out);
  and B01010 (B01010_out, not_5_out, in_2[1], not_3_out, in_2[3], not_1_out);
  and B01011 (B01011_out, in_2[0], in_2[1], not_3_out, in_2[3], not_1_out);
  and B01100 (B01100_out, not_5_out, not_4_out, in_2[2], in_2[3], not_1_out);
  and B01101 (B01101_out, in_2[0], not_4_out, in_2[2], in_2[3], not_1_out);
  and B01110 (B01110_out, not_5_out, in_2[1], in_2[2], in_2[3], not_1_out);
  and B01111 (B01111_out, in_2[0], in_2[1], in_2[2], in_2[3], not_1_out);
  and B10000 (B10000_out, not_5_out, not_4_out, not_3_out, not_2_out, in_2[4]);
  and B10001 (B10001_out, in_2[0], not_4_out, not_3_out, not_2_out, in_2[4]);
  and B10010 (B10010_out, not_5_out, in_2[1], not_3_out, not_2_out, in_2[4]);
  and B10011 (B10011_out, in_2[0], in_2[1], not_3_out, not_2_out, in_2[4]);
  and B10100 (B10100_out, not_5_out, not_4_out, in_2[2], not_2_out, in_2[4]);
  and B10101 (B10101_out, in_2[0], not_4_out, in_2[2], not_2_out, in_2[4]);
  and B10110 (B10110_out, not_5_out, in_2[1], in_2[2], not_2_out, in_2[4]);
  and B10111 (B10111_out, in_2[0], in_2[1], in_2[2], not_2_out, in_2[4]);
  and B11000 (B11000_out, not_5_out, not_4_out, not_3_out, in_2[3], in_2[4]);
  and B11001 (B11001_out, in_2[0], not_4_out, not_3_out, in_2[3], in_2[4]);
  and B11010 (B11010_out, not_5_out, in_2[1], not_3_out, in_2[3], in_2[4]);
  and B11011 (B11011_out, in_2[0], in_2[1], not_3_out, in_2[3], in_2[4]);
  and B11100 (B11100_out, not_5_out, not_4_out, in_2[2], in_2[3], in_2[4]);
  and B11101 (B11101_out, in_2[0], not_4_out, in_2[2], in_2[3], in_2[4]);
  and B11110 (B11110_out, not_5_out, in_2[1], in_2[2], in_2[3], in_2[4]);
  and B11111 (B11111_out, in_2[0], in_2[1], in_2[2], in_2[3], in_2[4]);
  and and_1 (and_1_out, in_4, B00000_out);
  and and_2 (and_2_out, in_4, B00001_out);
  and and_3 (and_3_out, in_4, B00010_out);
  and and_4 (and_4_out, in_4, B00011_out);
  and and_5 (and_5_out, in_4, B00100_out);
  and and_6 (and_6_out, in_4, B00101_out);
  and and_7 (and_7_out, in_4, B00110_out);
  and and_8 (and_8_out, in_4, B00111_out);
  and and_9 (and_9_out, in_4, B01000_out);
  and and_10 (and_10_out, in_4, B01001_out);
  and and_11 (and_11_out, in_4, B01010_out);
  and and_12 (and_12_out, in_4, B01011_out);
  and and_13 (and_13_out, in_4, B01100_out);
  and and_14 (and_14_out, in_4, B01101_out);
  and and_15 (and_15_out, in_4, B01110_out);
  and and_16 (and_16_out, in_4, B01111_out);
  and and_17 (and_17_out, in_4, B10000_out);
  and and_18 (and_18_out, in_4, B10001_out);
  and and_19 (and_19_out, in_4, B10010_out);
  and and_20 (and_20_out, in_4, B10011_out);
  and and_21 (and_21_out, in_4, B10100_out);
  and and_22 (and_22_out, in_4, B10101_out);
  and and_23 (and_23_out, in_4, B10110_out);
  and and_24 (and_24_out, in_4, B10111_out);
  and and_25 (and_25_out, in_4, B11000_out);
  and and_26 (and_26_out, in_4, B11001_out);
  and and_27 (and_27_out, in_4, B11010_out);
  and and_28 (and_28_out, in_4, B11011_out);
  and and_29 (and_29_out, in_4, B11100_out);
  and and_30 (and_30_out, in_4, B11101_out);
  and and_31 (and_31_out, in_4, B11110_out);
  and and_32 (and_32_out, in_4, B11111_out);
  Demultiplexer #(.select(5), .width(32)) demultiplexer_1 (
    .out0(demultiplexer_1_out0), .out1(demultiplexer_1_out1), .out2(demultiplexer_1_out2),
    .out3(demultiplexer_1_out3), .out4(demultiplexer_1_out4), .out5(demultiplexer_1_out5),
    .out6(demultiplexer_1_out6), .out7(demultiplexer_1_out7), .out8(demultiplexer_1_out8),
    .out9(demultiplexer_1_out9), .out10(demultiplexer_1_out10), .out11(demultiplexer_1_out11),
    .out12(demultiplexer_1_out12), .out13(demultiplexer_1_out13), .out14(demultiplexer_1_out14),
    .out15(demultiplexer_1_out15), .out16(demultiplexer_1_out16), .out17(demultiplexer_1_out17),
    .out18(demultiplexer_1_out18), .out19(demultiplexer_1_out19), .out20(demultiplexer_1_out20),
    .out21(demultiplexer_1_out21), .out22(demultiplexer_1_out22), .out23(demultiplexer_1_out23),
    .out24(demultiplexer_1_out24), .out25(demultiplexer_1_out25), .out26(demultiplexer_1_out26),
    .out27(demultiplexer_1_out27), .out28(demultiplexer_1_out28), .out29(demultiplexer_1_out29),
    .out30(demultiplexer_1_out30), .out31(demultiplexer_1_out31), .in(in_1));  // open: sel
  smallstuff smallstuff_1 (.selectionIN(in_17), .BitIN(demultiplexer_1_out21), .out_3(smallstuff_1_out_3));
  smallstuff smallstuff_2 (.selectionIN(in_19), .BitIN(demultiplexer_1_out22), .out_3(smallstuff_2_out_3));
  smallstuff smallstuff_3 (.selectionIN(in_20), .BitIN(demultiplexer_1_out23), .out_3(smallstuff_3_out_3));
  smallstuff smallstuff_4 (.selectionIN(in_18), .BitIN(demultiplexer_1_out7), .out_3(smallstuff_4_out_3));
  smallstuff smallstuff_5 (.selectionIN(in_21), .BitIN(demultiplexer_1_out8), .out_3(smallstuff_5_out_3));
  smallstuff smallstuff_6 (.selectionIN(in_30), .BitIN(demultiplexer_1_out13), .out_3(smallstuff_6_out_3));
  smallstuff smallstuff_7 (.selectionIN(in_32), .BitIN(demultiplexer_1_out14), .out_3(smallstuff_7_out_3));
  Clock clock_1 (.out(clock_1_out));
  smallstuff smallstuff_8 (.selectionIN(in_5), .BitIN(demultiplexer_1_out0), .out_3(smallstuff_8_out_3));
  smallstuff smallstuff_9 (.selectionIN(in_7), .BitIN(demultiplexer_1_out2), .out_3(smallstuff_9_out_3));
  smallstuff smallstuff_10 (.selectionIN(in_22), .BitIN(demultiplexer_1_out9), .out_3(smallstuff_10_out_3));
  smallstuff smallstuff_11 (.selectionIN(in_24), .BitIN(demultiplexer_1_out10), .out_3(smallstuff_11_out_3));
  smallstuff smallstuff_12 (.selectionIN(in_34), .BitIN(demultiplexer_1_out15), .out_3(smallstuff_12_out_3));
  smallstuff smallstuff_13 (.selectionIN(in_8), .BitIN(demultiplexer_1_out16), .out_3(smallstuff_13_out_3));
  smallstuff smallstuff_14 (.selectionIN(in_23), .BitIN(demultiplexer_1_out24), .out_3(smallstuff_14_out_3));
  smallstuff smallstuff_15 (.selectionIN(in_25), .BitIN(demultiplexer_1_out25), .out_3(smallstuff_15_out_3));
  smallstuff smallstuff_16 (.selectionIN(in_27), .BitIN(demultiplexer_1_out26), .out_3(smallstuff_16_out_3));
  smallstuff smallstuff_17 (.selectionIN(in_6), .BitIN(demultiplexer_1_out1), .out_3(smallstuff_17_out_3));
  smallstuff smallstuff_18 (.selectionIN(in_9), .BitIN(demultiplexer_1_out3), .out_3(smallstuff_18_out_3));
  smallstuff smallstuff_19 (.selectionIN(in_26), .BitIN(demultiplexer_1_out11), .out_3(demultiplexer_1_out20));
  smallstuff smallstuff_20 (.selectionIN(in_10), .BitIN(demultiplexer_1_out17), .out_3(smallstuff_20_out_3));
  smallstuff smallstuff_21 (.selectionIN(in_11), .BitIN(demultiplexer_1_out18), .out_3(smallstuff_21_out_3));
  smallstuff smallstuff_22 (.selectionIN(in_28), .BitIN(demultiplexer_1_out27), .out_3(smallstuff_22_out_3));
  smallstuff smallstuff_23 (.selectionIN(in_31), .BitIN(demultiplexer_1_out28), .out_3(smallstuff_23_out_3));
  smallstuff smallstuff_24 (.selectionIN(in_33), .BitIN(demultiplexer_1_out29), .out_3(smallstuff_24_out_3));
  smallstuff smallstuff_25 (.selectionIN(in_13), .BitIN(demultiplexer_1_out4), .out_3(smallstuff_25_out_3));
  smallstuff smallstuff_26 (.selectionIN(in_14), .BitIN(demultiplexer_1_out5), .out_3(smallstuff_26_out_3));
  smallstuff smallstuff_27 (.selectionIN(in_35), .BitIN(demultiplexer_1_out30), .out_3(smallstuff_27_out_3));
  smallstuff smallstuff_28 (.selectionIN(in_36), .BitIN(demultiplexer_1_out31), .out_3(smallstuff_28_out_3));
  smallstuff smallstuff_29 (.selectionIN(in_29), .BitIN(demultiplexer_1_out12), .out_3(smallstuff_29_out_3));
  smallstuff smallstuff_30 (.selectionIN(in_12), .BitIN(demultiplexer_1_out19), .out_3(smallstuff_30_out_3));
  smallstuff smallstuff_31 (.selectionIN(in_15), .BitIN(demultiplexer_1_out20), .out_3(smallstuff_31_out_3));
  smallstuff smallstuff_32 (.selectionIN(in_16), .BitIN(demultiplexer_1_out6), .out_3(smallstuff_32_out_3));
  Registers32 registers32_1 (
    .ENR0AllSet(and_1_out), .SelectionR0(in_5), .InputData(in_3), .CLK(clock_1_out), .ENR1AllSet(and_2_out),
    .SelectionR1(in_6), .ENR2AllSet(and_3_out), .SelectionR2(in_7), .ENR16AllSet(and_17_out),
    .SelectionR16(in_8), .ENR3AllSet3(and_4_out), .SelectionR3(in_9), .ENR17AllSet(and_18_out),
    .SelectionR17(in_10), .ENR18AllSet(and_19_out), .SelectionR18(in_11), .ENR19AllSet(and_20_out),
    .ENR0(smallstuff_8_out_3), .ENR1(smallstuff_17_out_3), .ENR2(smallstuff_9_out_3),
    .ENR3(smallstuff_18_out_3), .ENR16(smallstuff_13_out_3), .ENR17(smallstuff_20_out_3),
    .ENR18(smallstuff_21_out_3), .ENR19(smallstuff_30_out_3), .SelectionR19(in_12), .ENR4AllSet(and_5_out),
    .SelectionR4(in_13), .ENR5AllSet(and_6_out), .SelectionR5(in_14), .ENR20AllSet(and_21_out),
    .SelectionR20(in_15), .ENR6AllSet(and_7_out), .SelectionR6(in_16), .ENR21AllSet(and_22_out),
    .SelectionR21(in_17), .ENR7AllSet(and_8_out), .SelectionR7(in_18), .ENR22AllSet(and_23_out),
    .SelectionR22(in_19), .ENR23AllSet(and_24_out), .ENR4(smallstuff_25_out_3), .ENR5(smallstuff_26_out_3),
    .ENR6(smallstuff_32_out_3), .ENR7(smallstuff_4_out_3), .ENR20(smallstuff_31_out_3),
    .ENR21(smallstuff_1_out_3), .ENR22(smallstuff_2_out_3), .ENR23(smallstuff_3_out_3), .SelectionR23(in_20),
    .ENR8AllSet(and_9_out), .SelectionR8(in_21), .ENR9AllSet(and_10_out), .ENR24AllSet(and_25_out),
    .SelectionR9(in_22), .SelectionR24(in_23), .ENR10AllSet(and_11_out), .ENR25AllSet(and_26_out),
    .SelectionR10(in_24), .SelectionR25(in_25), .ENR11AllSet(and_12_out), .SelectionR11(in_26),
    .ENR26AllSet(and_27_out), .SelectionR26(in_27), .ENR27AllSet(and_28_out), .ENR8(smallstuff_5_out_3),
    .ENR9(smallstuff_10_out_3), .ENR10(smallstuff_11_out_3), .ENR11(demultiplexer_1_out20),
    .ENR24(smallstuff_14_out_3), .ENR25(smallstuff_15_out_3), .ENR26(smallstuff_16_out_3),
    .ENR27(smallstuff_22_out_3), .SelectionR27(in_28), .ENR12AllSet(and_13_out), .SelectionR12(in_29),
    .ENR13AllSet(and_14_out), .SelectionR13(in_30), .ENR28AllSet(and_29_out), .SelectionR28(in_31),
    .ENR14AllSet(and_15_out), .SelectionR14(in_32), .ENR29AllSet(and_30_out), .SelectionR29(in_33),
    .ENR15AllSet(and_16_out), .SelectionR15(in_34), .ENR30AllSet(and_31_out), .SelectionR30(in_35),
    .ENR31AllSet(and_32_out), .ENR12(smallstuff_29_out_3), .ENR13(smallstuff_6_out_3),
    .ENR14(smallstuff_7_out_3), .ENR15(smallstuff_12_out_3), .ENR28(smallstuff_23_out_3),
    .ENR29(smallstuff_24_out_3), .ENR30(smallstuff_27_out_3), .ENR31(smallstuff_28_out_3),
    .SelectionR31(in_36), .OutputR0(out_37));  // open: OutputR1, OutputR2, OutputR3, OutputR16, OutputR17, OutputR18, OutputR19, OutputR4, OutputR5, OutputR6, OutputR7, OutputR20, OutputR21, OutputR22, OutputR23, OutputR8, OutputR9, OutputR10, OutputR11, OutputR24, OutputR25, OutputR26, OutputR27, OutputR12, OutputR13, OutputR14, OutputR15, OutputR28, OutputR29, OutputR30, OutputR31
endmodule

module Registers32 (
  input  ENR0AllSet,
  input  SelectionR0,
  input  [31:0] InputData,
  input  CLK,
  input  ENR1AllSet,
  input  SelectionR1,
  input  ENR2AllSet,
  input  SelectionR2,
  input  ENR16AllSet,
  input  SelectionR16,
  input  ENR3AllSet3,
  input  SelectionR3,
  input  ENR17AllSet,
  input  SelectionR17,
  input  ENR18AllSet,
  input  SelectionR18,
  input  ENR19AllSet,
  input  [31:0] ENR0,
  input  [31:0] ENR1,
  input  [31:0] ENR2,
  input  [31:0] ENR3,
  input  [31:0] ENR16,
  input  [31:0] ENR17,
  input  [31:0] ENR18,
  input  [31:0] ENR19,
  input  SelectionR19,
  input  ENR4AllSet,
  input  SelectionR4,
  input  ENR5AllSet,
  input  SelectionR5,
  input  ENR20AllSet,
  input  SelectionR20,
  input  ENR6AllSet,
  input  SelectionR6,
  input  ENR21AllSet,
  input  SelectionR21,
  input  ENR7AllSet,
  input  SelectionR7,
  input  ENR22AllSet,
  input  SelectionR22,
  input  ENR23AllSet,
  input  [31:0] ENR4,
  input  [31:0] ENR5,
  input  [31:0] ENR6,
  input  [31:0] ENR7,
  input  [31:0] ENR20,
  input  [31:0] ENR21,
  input  [31:0] ENR22,
  input  [31:0] ENR23,
  input  SelectionR23,
  input  ENR8AllSet,
  input  SelectionR8,
  input  ENR9AllSet,
  input  ENR24AllSet,
  input  SelectionR9,
  input  SelectionR24,
  input  ENR10AllSet,
  input  ENR25AllSet,
  input  SelectionR10,
  input  SelectionR25,
  input  ENR11AllSet,
  input  SelectionR11,
  input  ENR26AllSet,
  input  SelectionR26,
  input  ENR27AllSet,
  input  [31:0] ENR8,
  input  [31:0] ENR9,
  input  [31:0] ENR10,
  input  [31:0] ENR11,
  input  [31:0] ENR24,
  input  [31:0] ENR25,
  input  [31:0] ENR26,
  input  [31:0] ENR27,
  input  SelectionR27,
  input  ENR12AllSet,
  input  SelectionR12,
  input  ENR13AllSet,
  input  SelectionR13,
  input  ENR28AllSet,
  input  SelectionR28,
  input  ENR14AllSet,
  input  SelectionR14,
  input  ENR29AllSet,
  input  SelectionR29,
  input  ENR15AllSet,
  input  SelectionR15,
  input  ENR30AllSet,
  input  SelectionR30,
  input  ENR31AllSet,
  input  [31:0] ENR12,
  input  [31:0] ENR13,
  input  [31:0] ENR14,
  input  [31:0] ENR15,
  input  [31:0] ENR28,
  input  [31:0] ENR29,
  input  [31:0] ENR30,
  input  [31:0] ENR31,
  input  SelectionR31,
  output [31:0] OutputR0,
  output [31:0] OutputR1,
  output [31:0] OutputR2,
  output [31:0] OutputR3,
  output [31:0] OutputR16,
  output [31:0] OutputR17,
  output [31:0] OutputR18,
  output [31:0] OutputR19,
  output [31:0] OutputR4,
  output [31:0] OutputR5,
  output [31:0] OutputR6,
  output [31:0] OutputR7,
  output [31:0] OutputR20,
  output [31:0] OutputR21,
  output [31:0] OutputR22,
  output [31:0] OutputR23,
  output [31:0] OutputR8,
  output [31:0] OutputR9,
  output [31:0] OutputR10,
  output [31:0] OutputR11,
  output [31:0] OutputR24,
  output [31:0] OutputR25,
  output [31:0] OutputR26,
  output [31:0] OutputR27,
  output [31:0] OutputR12,
  output [31:0] OutputR13,
  output [31:0] OutputR14,
  output [31:0] OutputR15,
  output [31:0] OutputR28,
  output [31:0] OutputR29,
  output [31:0] OutputR30,
  output [31:0] OutputR31
);

  wire nand_1_out, nand_2_out, nand_3_out, nand_4_out, nand_5_out, nand_6_out, nand_7_out, nand_8_out,
       nand_9_out, nand_10_out, nand_11_out, nand_12_out, nand_13_out, nand_14_out, nand_15_out, nand_16_out,
       nand_17_out, nand_18_out, nand_19_out, nand_20_out, nand_21_out, nand_22_out, nand_23_out,
       nand_24_out, nand_25_out, nand_26_out, nand_27_out, nand_28_out, nand_29_out, nand_30_out,
       nand_31_out, nand_32_out, not_1_out, not_2_out, not_3_out, not_4_out, not_5_out, not_6_out, not_7_out,
       not_8_out, not_9_out, not_10_out, not_11_out, not_12_out, not_13_out, not_14_out, not_15_out,
       not_16_out, not_17_out, not_18_out, not_19_out, not_20_out, not_21_out, not_22_out, not_23_out,
       not_24_out, not_25_out, not_26_out, not_27_out, not_28_out, not_29_out, not_30_out, not_31_out,
       not_32_out, xor_1_out, xor_2_out, xor_3_out, xor_4_out, xor_5_out, xor_6_out, xor_7_out, xor_8_out,
       xor_9_out, xor_10_out, xor_11_out, xor_12_out, xor_13_out, xor_14_out, xor_15_out, xor_16_out,
       xor_17_out, xor_18_out, xor_19_out, xor_20_out, xor_21_out, xor_22_out, xor_23_out, xor_24_out,
       xor_25_out, xor_26_out, xor_27_out, xor_28_out, xor_29_out, xor_30_out, xor_31_out, xor_32_out;
  wire [31:0] multiplexer_1_out, multiplexer_2_out, multiplexer_3_out, multiplexer_4_out, multiplexer_5_out,
       multiplexer_6_out, multiplexer_7_out, multiplexer_8_out, multiplexer_9_out, multiplexer_10_out,
       multiplexer_11_out, multiplexer_12_out, multiplexer_13_out, multiplexer_14_out, multiplexer_15_out,
       multiplexer_16_out, multiplexer_17_out, multiplexer_18_out, multiplexer_19_out, multiplexer_20_out,
       multiplexer_21_out, multiplexer_22_out, multiplexer_23_out, multiplexer_24_out, multiplexer_25_out,
       multiplexer_26_out, multiplexer_27_out, multiplexer_28_out, multiplexer_29_out, multiplexer_30_out,
       multiplexer_31_out, multiplexer_32_out;

  not not_1 (not_1_out, SelectionR13);
  not not_2 (not_2_out, SelectionR0);
  not not_3 (not_3_out, SelectionR1);
  not not_4 (not_4_out, SelectionR2);
  not not_5 (not_5_out, SelectionR3);
  not not_6 (not_6_out, SelectionR4);
  xor xor_1 (xor_1_out, ENR5AllSet, SelectionR5);
  not not_7 (not_7_out, SelectionR5);
  xor xor_2 (xor_2_out, ENR6AllSet, SelectionR6);
  not not_8 (not_8_out, SelectionR6);
  xor xor_3 (xor_3_out, ENR7AllSet, SelectionR7);
  not not_9 (not_9_out, SelectionR7);
  xor xor_4 (xor_4_out, ENR8AllSet, SelectionR8);
  not not_10 (not_10_out, SelectionR8);
  xor xor_5 (xor_5_out, ENR9AllSet, SelectionR9);
  not not_11 (not_11_out, SelectionR9);
  xor xor_6 (xor_6_out, ENR10AllSet, SelectionR10);
  not not_12 (not_12_out, SelectionR10);
  xor xor_7 (xor_7_out, ENR11AllSet, SelectionR11);
  not not_13 (not_13_out, SelectionR11);
  xor xor_8 (xor_8_out, ENR12AllSet, SelectionR12);
  not not_14 (not_14_out, SelectionR12);
  xor xor_9 (xor_9_out, ENR13AllSet, SelectionR13);
  xor xor_10 (xor_10_out, ENR14AllSet, SelectionR14);
  not not_15 (not_15_out, SelectionR14);
  xor xor_11 (xor_11_out, ENR15AllSet, SelectionR15);
  not not_16 (not_16_out, SelectionR15);
  xor xor_12 (xor_12_out, ENR0AllSet, SelectionR0);
  xor xor_13 (xor_13_out, ENR1AllSet, SelectionR1);
  xor xor_14 (xor_14_out, ENR2AllSet, SelectionR2);
  xor xor_15 (xor_15_out, ENR3AllSet3, SelectionR3);
  xor xor_16 (xor_16_out, ENR4AllSet, SelectionR4);
  nand nand_1 (nand_1_out, xor_5_out, not_11_out);
  nand nand_2 (nand_2_out, xor_9_out, not_1_out);
  nand nand_3 (nand_3_out, xor_10_out, not_15_out);
  nand nand_4 (nand_4_out, xor_11_out, not_16_out);
  nand nand_5 (nand_5_out, xor_12_out, not_2_out);
  nand nand_6 (nand_6_out, xor_13_out, not_3_out);
  nand nand_7 (nand_7_out, xor_14_out, not_4_out);
  nand nand_8 (nand_8_out, xor_15_out, not_5_out);
  nand nand_9 (nand_9_out, xor_16_out, not_6_out);
  nand nand_10 (nand_10_out, xor_1_out, not_7_out);
  nand nand_11 (nand_11_out, xor_2_out, not_8_out);
  nand nand_12 (nand_12_out, xor_3_out, not_9_out);
  nand nand_13 (nand_13_out, xor_4_out, not_10_out);
  nand nand_14 (nand_14_out, xor_6_out, not_12_out);
  nand nand_15 (nand_15_out, xor_7_out, not_13_out);
  nand nand_16 (nand_16_out, xor_8_out, not_14_out);
  Multiplexer #(.width(32)) multiplexer_1 (
    .in0({32{ENR0AllSet}}), .in1(ENR0), .out(multiplexer_1_out), .sel(nand_5_out));
  Multiplexer #(.width(32)) multiplexer_2 (
    .in0({32{ENR4AllSet}}), .in1(ENR4), .out(multiplexer_2_out), .sel(nand_9_out));
  Multiplexer #(.width(32)) multiplexer_3 (
    .in0({32{ENR8AllSet}}), .in1(ENR8), .out(multiplexer_3_out), .sel(nand_13_out));
  Multiplexer #(.width(32)) multiplexer_4 (
    .in0({32{ENR12AllSet}}), .in1(ENR12), .out(multiplexer_4_out), .sel(nand_16_out));
  Register32Bit register32bit_1 (
    .EN0(multiplexer_1_out[0]), .EN1(multiplexer_1_out[1]), .clk(CLK), .EN2(multiplexer_1_out[2]),
    .EN3(multiplexer_1_out[3]), .InputData(InputData), .EN16(multiplexer_1_out[16]),
    .EN17(multiplexer_1_out[17]), .EN4(multiplexer_1_out[4]), .EN5(multiplexer_1_out[5]),
    .EN6(multiplexer_1_out[6]), .EN7(multiplexer_1_out[7]), .EN18(multiplexer_1_out[18]),
    .EN19(multiplexer_1_out[19]), .EN8(multiplexer_1_out[8]), .EN9(multiplexer_1_out[9]),
    .EN20(multiplexer_1_out[20]), .EN21(multiplexer_1_out[21]), .EN10(multiplexer_1_out[10]),
    .EN11(multiplexer_1_out[11]), .EN22(multiplexer_1_out[22]), .EN23(multiplexer_1_out[23]),
    .EN12(multiplexer_1_out[12]), .EN13(multiplexer_1_out[13]), .EN24(multiplexer_1_out[24]),
    .EN25(multiplexer_1_out[25]), .EN14(multiplexer_1_out[14]), .EN15(multiplexer_1_out[15]),
    .EN26(multiplexer_1_out[26]), .EN27(multiplexer_1_out[27]), .EN28(multiplexer_1_out[28]),
    .EN29(multiplexer_1_out[29]), .EN30(multiplexer_1_out[30]), .EN31(multiplexer_1_out[31]),
    .OutputData(OutputR0));
  Register32Bit register32bit_2 (
    .EN0(multiplexer_2_out[0]), .EN1(multiplexer_2_out[1]), .clk(CLK), .EN2(multiplexer_2_out[2]),
    .EN3(multiplexer_2_out[3]), .InputData(InputData), .EN16(multiplexer_2_out[16]),
    .EN17(multiplexer_2_out[17]), .EN4(multiplexer_2_out[4]), .EN5(multiplexer_2_out[5]),
    .EN6(multiplexer_2_out[6]), .EN7(multiplexer_2_out[7]), .EN18(multiplexer_2_out[18]),
    .EN19(multiplexer_2_out[19]), .EN8(multiplexer_2_out[8]), .EN9(multiplexer_2_out[9]),
    .EN20(multiplexer_2_out[20]), .EN21(multiplexer_2_out[21]), .EN10(multiplexer_2_out[10]),
    .EN11(multiplexer_2_out[11]), .EN22(multiplexer_2_out[22]), .EN23(multiplexer_2_out[23]),
    .EN12(multiplexer_2_out[12]), .EN13(multiplexer_2_out[13]), .EN24(multiplexer_2_out[24]),
    .EN25(multiplexer_2_out[25]), .EN14(multiplexer_2_out[14]), .EN15(multiplexer_2_out[15]),
    .EN26(multiplexer_2_out[26]), .EN27(multiplexer_2_out[27]), .EN28(multiplexer_2_out[28]),
    .EN29(multiplexer_2_out[29]), .EN30(multiplexer_2_out[30]), .EN31(multiplexer_2_out[31]),
    .OutputData(OutputR4));
  Register32Bit register32bit_3 (
    .EN0(multiplexer_3_out[0]), .EN1(multiplexer_3_out[1]), .clk(CLK), .EN2(multiplexer_3_out[2]),
    .EN3(multiplexer_3_out[3]), .InputData(InputData), .EN16(multiplexer_3_out[16]),
    .EN17(multiplexer_3_out[17]), .EN4(multiplexer_3_out[4]), .EN5(multiplexer_3_out[5]),
    .EN6(multiplexer_3_out[6]), .EN7(multiplexer_3_out[7]), .EN18(multiplexer_3_out[18]),
    .EN19(multiplexer_3_out[19]), .EN8(multiplexer_3_out[8]), .EN9(multiplexer_3_out[9]),
    .EN20(multiplexer_3_out[20]), .EN21(multiplexer_3_out[21]), .EN10(multiplexer_3_out[10]),
    .EN11(multiplexer_3_out[11]), .EN22(multiplexer_3_out[22]), .EN23(multiplexer_3_out[23]),
    .EN12(multiplexer_3_out[12]), .EN13(multiplexer_3_out[13]), .EN24(multiplexer_3_out[24]),
    .EN25(multiplexer_3_out[25]), .EN14(multiplexer_3_out[14]), .EN15(multiplexer_3_out[15]),
    .EN26(multiplexer_3_out[26]), .EN27(multiplexer_3_out[27]), .EN28(multiplexer_3_out[28]),
    .EN29(multiplexer_3_out[29]), .EN30(multiplexer_3_out[30]), .EN31(multiplexer_3_out[31]),
    .OutputData(OutputR8));
  Register32Bit register32bit_4 (
    .EN0(multiplexer_4_out[0]), .EN1(multiplexer_4_out[1]), .clk(CLK), .EN2(multiplexer_4_out[2]),
    .EN3(multiplexer_4_out[3]), .InputData(InputData), .EN16(multiplexer_4_out[16]),
    .EN17(multiplexer_4_out[17]), .EN4(multiplexer_4_out[4]), .EN5(multiplexer_4_out[5]),
    .EN6(multiplexer_4_out[6]), .EN7(multiplexer_4_out[7]), .EN18(multiplexer_4_out[18]),
    .EN19(multiplexer_4_out[19]), .EN8(multiplexer_4_out[8]), .EN9(multiplexer_4_out[9]),
    .EN20(multiplexer_4_out[20]), .EN21(multiplexer_4_out[21]), .EN10(multiplexer_4_out[10]),
    .EN11(multiplexer_4_out[11]), .EN22(multiplexer_4_out[22]), .EN23(multiplexer_4_out[23]),
    .EN12(multiplexer_4_out[12]), .EN13(multiplexer_4_out[13]), .EN24(multiplexer_4_out[24]),
    .EN25(multiplexer_4_out[25]), .EN14(multiplexer_4_out[14]), .EN15(multiplexer_4_out[15]),
    .EN26(multiplexer_4_out[26]), .EN27(multiplexer_4_out[27]), .EN28(multiplexer_4_out[28]),
    .EN29(multiplexer_4_out[29]), .EN30(multiplexer_4_out[30]), .EN31(multiplexer_4_out[31]),
    .OutputData(OutputR12));
  Multiplexer #(.width(32)) multiplexer_5 (
    .in0({32{ENR1AllSet}}), .in1(ENR1), .out(multiplexer_5_out), .sel(nand_6_out));
  Multiplexer #(.width(32)) multiplexer_6 (
    .in0({32{ENR5AllSet}}), .in1(ENR5), .out(multiplexer_6_out), .sel(nand_10_out));
  Multiplexer #(.width(32)) multiplexer_7 (
    .in0({32{ENR9AllSet}}), .in1(ENR9), .out(multiplexer_7_out), .sel(nand_1_out));
  Multiplexer #(.width(32)) multiplexer_8 (
    .in0({32{ENR13AllSet}}), .in1(ENR13), .out(multiplexer_8_out), .sel(nand_2_out));
  Register32Bit register32bit_5 (
    .EN0(multiplexer_5_out[0]), .EN1(multiplexer_5_out[1]), .clk(CLK), .EN2(multiplexer_5_out[2]),
    .EN3(multiplexer_5_out[3]), .InputData(InputData), .EN16(multiplexer_5_out[16]),
    .EN17(multiplexer_5_out[17]), .EN4(multiplexer_5_out[4]), .EN5(multiplexer_5_out[5]),
    .EN6(multiplexer_5_out[6]), .EN7(multiplexer_5_out[7]), .EN18(multiplexer_5_out[18]),
    .EN19(multiplexer_5_out[19]), .EN8(multiplexer_5_out[8]), .EN9(multiplexer_5_out[9]),
    .EN20(multiplexer_5_out[20]), .EN21(multiplexer_5_out[21]), .EN10(multiplexer_5_out[10]),
    .EN11(multiplexer_5_out[11]), .EN22(multiplexer_5_out[22]), .EN23(multiplexer_5_out[23]),
    .EN12(multiplexer_5_out[12]), .EN13(multiplexer_5_out[13]), .EN24(multiplexer_5_out[24]),
    .EN25(multiplexer_5_out[25]), .EN14(multiplexer_5_out[14]), .EN15(multiplexer_5_out[15]),
    .EN26(multiplexer_5_out[26]), .EN27(multiplexer_5_out[27]), .EN28(multiplexer_5_out[28]),
    .EN29(multiplexer_5_out[29]), .EN30(multiplexer_5_out[30]), .EN31(multiplexer_5_out[31]),
    .OutputData(OutputR1));
  Register32Bit register32bit_6 (
    .EN0(multiplexer_6_out[0]), .EN1(multiplexer_6_out[1]), .clk(CLK), .EN2(multiplexer_6_out[2]),
    .EN3(multiplexer_6_out[3]), .InputData(InputData), .EN16(multiplexer_6_out[16]),
    .EN17(multiplexer_6_out[17]), .EN4(multiplexer_6_out[4]), .EN5(multiplexer_6_out[5]),
    .EN6(multiplexer_6_out[6]), .EN7(multiplexer_6_out[7]), .EN18(multiplexer_6_out[18]),
    .EN19(multiplexer_6_out[19]), .EN8(multiplexer_6_out[8]), .EN9(multiplexer_6_out[9]),
    .EN20(multiplexer_6_out[20]), .EN21(multiplexer_6_out[21]), .EN10(multiplexer_6_out[10]),
    .EN11(multiplexer_6_out[11]), .EN22(multiplexer_6_out[22]), .EN23(multiplexer_6_out[23]),
    .EN12(multiplexer_6_out[12]), .EN13(multiplexer_6_out[13]), .EN24(multiplexer_6_out[24]),
    .EN25(multiplexer_6_out[25]), .EN14(multiplexer_6_out[14]), .EN15(multiplexer_6_out[15]),
    .EN26(multiplexer_6_out[26]), .EN27(multiplexer_6_out[27]), .EN28(multiplexer_6_out[28]),
    .EN29(multiplexer_6_out[29]), .EN30(multiplexer_6_out[30]), .EN31(multiplexer_6_out[31]),
    .OutputData(OutputR5));
  Register32Bit register32bit_7 (
    .EN0(multiplexer_7_out[0]), .EN1(multiplexer_7_out[1]), .clk(CLK), .EN2(multiplexer_7_out[2]),
    .EN3(multiplexer_7_out[3]), .InputData(InputData), .EN16(multiplexer_7_out[16]),
    .EN17(multiplexer_7_out[17]), .EN4(multiplexer_7_out[4]), .EN5(multiplexer_7_out[5]),
    .EN6(multiplexer_7_out[6]), .EN7(multiplexer_7_out[7]), .EN18(multiplexer_7_out[18]),
    .EN19(multiplexer_7_out[19]), .EN8(multiplexer_7_out[8]), .EN9(multiplexer_7_out[9]),
    .EN20(multiplexer_7_out[20]), .EN21(multiplexer_7_out[21]), .EN10(multiplexer_7_out[10]),
    .EN11(multiplexer_7_out[11]), .EN22(multiplexer_7_out[22]), .EN23(multiplexer_7_out[23]),
    .EN12(multiplexer_7_out[12]), .EN13(multiplexer_7_out[13]), .EN24(multiplexer_7_out[24]),
    .EN25(multiplexer_7_out[25]), .EN14(multiplexer_7_out[14]), .EN15(multiplexer_7_out[15]),
    .EN26(multiplexer_7_out[26]), .EN27(multiplexer_7_out[27]), .EN28(multiplexer_7_out[28]),
    .EN29(multiplexer_7_out[29]), .EN30(multiplexer_7_out[30]), .EN31(multiplexer_7_out[31]),
    .OutputData(OutputR9));
  Register32Bit register32bit_8 (
    .EN0(multiplexer_8_out[0]), .EN1(multiplexer_8_out[1]), .clk(CLK), .EN2(multiplexer_8_out[2]),
    .EN3(multiplexer_8_out[3]), .InputData(InputData), .EN16(multiplexer_8_out[16]),
    .EN17(multiplexer_8_out[17]), .EN4(multiplexer_8_out[4]), .EN5(multiplexer_8_out[5]),
    .EN6(multiplexer_8_out[6]), .EN7(multiplexer_8_out[7]), .EN18(multiplexer_8_out[18]),
    .EN19(multiplexer_8_out[19]), .EN8(multiplexer_8_out[8]), .EN9(multiplexer_8_out[9]),
    .EN20(multiplexer_8_out[20]), .EN21(multiplexer_8_out[21]), .EN10(multiplexer_8_out[10]),
    .EN11(multiplexer_8_out[11]), .EN22(multiplexer_8_out[22]), .EN23(multiplexer_8_out[23]),
    .EN12(multiplexer_8_out[12]), .EN13(multiplexer_8_out[13]), .EN24(multiplexer_8_out[24]),
    .EN25(multiplexer_8_out[25]), .EN14(multiplexer_8_out[14]), .EN15(multiplexer_8_out[15]),
    .EN26(multiplexer_8_out[26]), .EN27(multiplexer_8_out[27]), .EN28(multiplexer_8_out[28]),
    .EN29(multiplexer_8_out[29]), .EN30(multiplexer_8_out[30]), .EN31(multiplexer_8_out[31]),
    .OutputData(OutputR13));
  Multiplexer #(.width(32)) multiplexer_9 (
    .in0({32{ENR2AllSet}}), .in1(ENR2), .out(multiplexer_9_out), .sel(nand_7_out));
  Multiplexer #(.width(32)) multiplexer_10 (
    .in0({32{ENR6AllSet}}), .in1(ENR6), .out(multiplexer_10_out), .sel(nand_11_out));
  Multiplexer #(.width(32)) multiplexer_11 (
    .in0({32{ENR10AllSet}}), .in1(ENR10), .out(multiplexer_11_out), .sel(nand_14_out));
  Multiplexer #(.width(32)) multiplexer_12 (
    .in0({32{ENR14AllSet}}), .in1(ENR14), .out(multiplexer_12_out), .sel(nand_3_out));
  Register32Bit register32bit_9 (
    .EN0(multiplexer_9_out[0]), .EN1(multiplexer_9_out[1]), .clk(CLK), .EN2(multiplexer_9_out[2]),
    .EN3(multiplexer_9_out[3]), .InputData(InputData), .EN16(multiplexer_9_out[16]),
    .EN17(multiplexer_9_out[17]), .EN4(multiplexer_9_out[4]), .EN5(multiplexer_9_out[5]),
    .EN6(multiplexer_9_out[6]), .EN7(multiplexer_9_out[7]), .EN18(multiplexer_9_out[18]),
    .EN19(multiplexer_9_out[19]), .EN8(multiplexer_9_out[8]), .EN9(multiplexer_9_out[9]),
    .EN20(multiplexer_9_out[20]), .EN21(multiplexer_9_out[21]), .EN10(multiplexer_9_out[10]),
    .EN11(multiplexer_9_out[11]), .EN22(multiplexer_9_out[22]), .EN23(multiplexer_9_out[23]),
    .EN12(multiplexer_9_out[12]), .EN13(multiplexer_9_out[13]), .EN24(multiplexer_9_out[24]),
    .EN25(multiplexer_9_out[25]), .EN14(multiplexer_9_out[14]), .EN15(multiplexer_9_out[15]),
    .EN26(multiplexer_9_out[26]), .EN27(multiplexer_9_out[27]), .EN28(multiplexer_9_out[28]),
    .EN29(multiplexer_9_out[29]), .EN30(multiplexer_9_out[30]), .EN31(multiplexer_9_out[31]),
    .OutputData(OutputR2));
  Register32Bit register32bit_10 (
    .EN0(multiplexer_10_out[0]), .EN1(multiplexer_10_out[1]), .clk(CLK), .EN2(multiplexer_10_out[2]),
    .EN3(multiplexer_10_out[3]), .InputData(InputData), .EN16(multiplexer_10_out[16]),
    .EN17(multiplexer_10_out[17]), .EN4(multiplexer_10_out[4]), .EN5(multiplexer_10_out[5]),
    .EN6(multiplexer_10_out[6]), .EN7(multiplexer_10_out[7]), .EN18(multiplexer_10_out[18]),
    .EN19(multiplexer_10_out[19]), .EN8(multiplexer_10_out[8]), .EN9(multiplexer_10_out[9]),
    .EN20(multiplexer_10_out[20]), .EN21(multiplexer_10_out[21]), .EN10(multiplexer_10_out[10]),
    .EN11(multiplexer_10_out[11]), .EN22(multiplexer_10_out[22]), .EN23(multiplexer_10_out[23]),
    .EN12(multiplexer_10_out[12]), .EN13(multiplexer_10_out[13]), .EN24(multiplexer_10_out[24]),
    .EN25(multiplexer_10_out[25]), .EN14(multiplexer_10_out[14]), .EN15(multiplexer_10_out[15]),
    .EN26(multiplexer_10_out[26]), .EN27(multiplexer_10_out[27]), .EN28(multiplexer_10_out[28]),
    .EN29(multiplexer_10_out[29]), .EN30(multiplexer_10_out[30]), .EN31(multiplexer_10_out[31]),
    .OutputData(OutputR6));
  Register32Bit register32bit_11 (
    .EN0(multiplexer_11_out[0]), .EN1(multiplexer_11_out[1]), .clk(CLK), .EN2(multiplexer_11_out[2]),
    .EN3(multiplexer_11_out[3]), .InputData(InputData), .EN16(multiplexer_11_out[16]),
    .EN17(multiplexer_11_out[17]), .EN4(multiplexer_11_out[4]), .EN5(multiplexer_11_out[5]),
    .EN6(multiplexer_11_out[6]), .EN7(multiplexer_11_out[7]), .EN18(multiplexer_11_out[18]),
    .EN19(multiplexer_11_out[19]), .EN8(multiplexer_11_out[8]), .EN9(multiplexer_11_out[9]),
    .EN20(multiplexer_11_out[20]), .EN21(multiplexer_11_out[21]), .EN10(multiplexer_11_out[10]),
    .EN11(multiplexer_11_out[11]), .EN22(multiplexer_11_out[22]), .EN23(multiplexer_11_out[23]),
    .EN12(multiplexer_11_out[12]), .EN13(multiplexer_11_out[13]), .EN24(multiplexer_11_out[24]),
    .EN25(multiplexer_11_out[25]), .EN14(multiplexer_11_out[14]), .EN15(multiplexer_11_out[15]),
    .EN26(multiplexer_11_out[26]), .EN27(multiplexer_11_out[27]), .EN28(multiplexer_11_out[28]),
    .EN29(multiplexer_11_out[29]), .EN30(multiplexer_11_out[30]), .EN31(multiplexer_11_out[31]),
    .OutputData(OutputR10));
  Register32Bit register32bit_12 (
    .EN0(multiplexer_12_out[0]), .EN1(multiplexer_12_out[1]), .clk(CLK), .EN2(multiplexer_12_out[2]),
    .EN3(multiplexer_12_out[3]), .InputData(InputData), .EN16(multiplexer_12_out[16]),
    .EN17(multiplexer_12_out[17]), .EN4(multiplexer_12_out[4]), .EN5(multiplexer_12_out[5]),
    .EN6(multiplexer_12_out[6]), .EN7(multiplexer_12_out[7]), .EN18(multiplexer_12_out[18]),
    .EN19(multiplexer_12_out[19]), .EN8(multiplexer_12_out[8]), .EN9(multiplexer_12_out[9]),
    .EN20(multiplexer_12_out[20]), .EN21(multiplexer_12_out[21]), .EN10(multiplexer_12_out[10]),
    .EN11(multiplexer_12_out[11]), .EN22(multiplexer_12_out[22]), .EN23(multiplexer_12_out[23]),
    .EN12(multiplexer_12_out[12]), .EN13(multiplexer_12_out[13]), .EN24(multiplexer_12_out[24]),
    .EN25(multiplexer_12_out[25]), .EN14(multiplexer_12_out[14]), .EN15(multiplexer_12_out[15]),
    .EN26(multiplexer_12_out[26]), .EN27(multiplexer_12_out[27]), .EN28(multiplexer_12_out[28]),
    .EN29(multiplexer_12_out[29]), .EN30(multiplexer_12_out[30]), .EN31(multiplexer_12_out[31]),
    .OutputData(OutputR14));
  Multiplexer #(.width(32)) multiplexer_13 (
    .in0({32{ENR3AllSet3}}), .in1(ENR3), .out(multiplexer_13_out), .sel(nand_8_out));
  Multiplexer #(.width(32)) multiplexer_14 (
    .in0({32{ENR7AllSet}}), .in1(ENR7), .out(multiplexer_14_out), .sel(nand_12_out));
  Multiplexer #(.width(32)) multiplexer_15 (
    .in0({32{ENR11AllSet}}), .in1(ENR11), .out(multiplexer_15_out), .sel(nand_15_out));
  Multiplexer #(.width(32)) multiplexer_16 (
    .in0({32{ENR15AllSet}}), .in1(ENR15), .out(multiplexer_16_out), .sel(nand_4_out));
  Register32Bit register32bit_13 (
    .EN0(multiplexer_13_out[0]), .EN1(multiplexer_13_out[1]), .clk(CLK), .EN2(multiplexer_13_out[2]),
    .EN3(multiplexer_13_out[3]), .InputData(InputData), .EN16(multiplexer_13_out[16]),
    .EN17(multiplexer_13_out[17]), .EN4(multiplexer_13_out[4]), .EN5(multiplexer_13_out[5]),
    .EN6(multiplexer_13_out[6]), .EN7(multiplexer_13_out[7]), .EN18(multiplexer_13_out[18]),
    .EN19(multiplexer_13_out[19]), .EN8(multiplexer_13_out[8]), .EN9(multiplexer_13_out[9]),
    .EN20(multiplexer_13_out[20]), .EN21(multiplexer_13_out[21]), .EN10(multiplexer_13_out[10]),
    .EN11(multiplexer_13_out[11]), .EN22(multiplexer_13_out[22]), .EN23(multiplexer_13_out[23]),
    .EN12(multiplexer_13_out[12]), .EN13(multiplexer_13_out[13]), .EN24(multiplexer_13_out[24]),
    .EN25(multiplexer_13_out[25]), .EN14(multiplexer_13_out[14]), .EN15(multiplexer_13_out[15]),
    .EN26(multiplexer_13_out[26]), .EN27(multiplexer_13_out[27]), .EN28(multiplexer_13_out[28]),
    .EN29(multiplexer_13_out[29]), .EN30(multiplexer_13_out[30]), .EN31(multiplexer_13_out[31]),
    .OutputData(OutputR3));
  Register32Bit register32bit_14 (
    .EN0(multiplexer_14_out[0]), .EN1(multiplexer_14_out[1]), .clk(CLK), .EN2(multiplexer_14_out[2]),
    .EN3(multiplexer_14_out[3]), .InputData(InputData), .EN16(multiplexer_14_out[16]),
    .EN17(multiplexer_14_out[17]), .EN4(multiplexer_14_out[4]), .EN5(multiplexer_14_out[5]),
    .EN6(multiplexer_14_out[6]), .EN7(multiplexer_14_out[7]), .EN18(multiplexer_14_out[18]),
    .EN19(multiplexer_14_out[19]), .EN8(multiplexer_14_out[8]), .EN9(multiplexer_14_out[9]),
    .EN20(multiplexer_14_out[20]), .EN21(multiplexer_14_out[21]), .EN10(multiplexer_14_out[10]),
    .EN11(multiplexer_14_out[11]), .EN22(multiplexer_14_out[22]), .EN23(multiplexer_14_out[23]),
    .EN12(multiplexer_14_out[12]), .EN13(multiplexer_14_out[13]), .EN24(multiplexer_14_out[24]),
    .EN25(multiplexer_14_out[25]), .EN14(multiplexer_14_out[14]), .EN15(multiplexer_14_out[15]),
    .EN26(multiplexer_14_out[26]), .EN27(multiplexer_14_out[27]), .EN28(multiplexer_14_out[28]),
    .EN29(multiplexer_14_out[29]), .EN30(multiplexer_14_out[30]), .EN31(multiplexer_14_out[31]),
    .OutputData(OutputR7));
  Register32Bit register32bit_15 (
    .EN0(multiplexer_15_out[0]), .EN1(multiplexer_15_out[1]), .clk(CLK), .EN2(multiplexer_15_out[2]),
    .EN3(multiplexer_15_out[3]), .InputData(InputData), .EN16(multiplexer_15_out[16]),
    .EN17(multiplexer_15_out[17]), .EN4(multiplexer_15_out[4]), .EN5(multiplexer_15_out[5]),
    .EN6(multiplexer_15_out[6]), .EN7(multiplexer_15_out[7]), .EN18(multiplexer_15_out[18]),
    .EN19(multiplexer_15_out[19]), .EN8(multiplexer_15_out[8]), .EN9(multiplexer_15_out[9]),
    .EN20(multiplexer_15_out[20]), .EN21(multiplexer_15_out[21]), .EN10(multiplexer_15_out[10]),
    .EN11(multiplexer_15_out[11]), .EN22(multiplexer_15_out[22]), .EN23(multiplexer_15_out[23]),
    .EN12(multiplexer_15_out[12]), .EN13(multiplexer_15_out[13]), .EN24(multiplexer_15_out[24]),
    .EN25(multiplexer_15_out[25]), .EN14(multiplexer_15_out[14]), .EN15(multiplexer_15_out[15]),
    .EN26(multiplexer_15_out[26]), .EN27(multiplexer_15_out[27]), .EN28(multiplexer_15_out[28]),
    .EN29(multiplexer_15_out[29]), .EN30(multiplexer_15_out[30]), .EN31(multiplexer_15_out[31]),
    .OutputData(OutputR11));
  Register32Bit register32bit_16 (
    .EN0(multiplexer_16_out[0]), .EN1(multiplexer_16_out[1]), .clk(CLK), .EN2(multiplexer_16_out[2]),
    .EN3(multiplexer_16_out[3]), .InputData(InputData), .EN16(multiplexer_16_out[16]),
    .EN17(multiplexer_16_out[17]), .EN4(multiplexer_16_out[4]), .EN5(multiplexer_16_out[5]),
    .EN6(multiplexer_16_out[6]), .EN7(multiplexer_16_out[7]), .EN18(multiplexer_16_out[18]),
    .EN19(multiplexer_16_out[19]), .EN8(multiplexer_16_out[8]), .EN9(multiplexer_16_out[9]),
    .EN20(multiplexer_16_out[20]), .EN21(multiplexer_16_out[21]), .EN10(multiplexer_16_out[10]),
    .EN11(multiplexer_16_out[11]), .EN22(multiplexer_16_out[22]), .EN23(multiplexer_16_out[23]),
    .EN12(multiplexer_16_out[12]), .EN13(multiplexer_16_out[13]), .EN24(multiplexer_16_out[24]),
    .EN25(multiplexer_16_out[25]), .EN14(multiplexer_16_out[14]), .EN15(multiplexer_16_out[15]),
    .EN26(multiplexer_16_out[26]), .EN27(multiplexer_16_out[27]), .EN28(multiplexer_16_out[28]),
    .EN29(multiplexer_16_out[29]), .EN30(multiplexer_16_out[30]), .EN31(multiplexer_16_out[31]),
    .OutputData(OutputR15));
  Multiplexer #(.width(32)) multiplexer_17 (
    .in0({32{ENR16AllSet}}), .in1(ENR16), .out(multiplexer_17_out), .sel(nand_26_out));
  Multiplexer #(.width(32)) multiplexer_18 (
    .in0({32{ENR20AllSet}}), .in1(ENR20), .out(multiplexer_18_out), .sel(nand_30_out));
  Multiplexer #(.width(32)) multiplexer_19 (
    .in0({32{ENR24AllSet}}), .in1(ENR24), .out(multiplexer_19_out), .sel(nand_18_out));
  Multiplexer #(.width(32)) multiplexer_20 (
    .in0({32{ENR28AllSet}}), .in1(ENR28), .out(multiplexer_20_out), .sel(nand_22_out));
  Register32Bit register32bit_17 (
    .EN0(multiplexer_17_out[0]), .EN1(multiplexer_17_out[1]), .clk(CLK), .EN2(multiplexer_17_out[2]),
    .EN3(multiplexer_17_out[3]), .InputData(InputData), .EN16(multiplexer_17_out[16]),
    .EN17(multiplexer_17_out[17]), .EN4(multiplexer_17_out[4]), .EN5(multiplexer_17_out[5]),
    .EN6(multiplexer_17_out[6]), .EN7(multiplexer_17_out[7]), .EN18(multiplexer_17_out[18]),
    .EN19(multiplexer_17_out[19]), .EN8(multiplexer_17_out[8]), .EN9(multiplexer_17_out[9]),
    .EN20(multiplexer_17_out[20]), .EN21(multiplexer_17_out[21]), .EN10(multiplexer_17_out[10]),
    .EN11(multiplexer_17_out[11]), .EN22(multiplexer_17_out[22]), .EN23(multiplexer_17_out[23]),
    .EN12(multiplexer_17_out[12]), .EN13(multiplexer_17_out[13]), .EN24(multiplexer_17_out[24]),
    .EN25(multiplexer_17_out[25]), .EN14(multiplexer_17_out[14]), .EN15(multiplexer_17_out[15]),
    .EN26(multiplexer_17_out[26]), .EN27(multiplexer_17_out[27]), .EN28(multiplexer_17_out[28]),
    .EN29(multiplexer_17_out[29]), .EN30(multiplexer_17_out[30]), .EN31(multiplexer_17_out[31]),
    .OutputData(OutputR16));
  Register32Bit register32bit_18 (
    .EN0(multiplexer_18_out[0]), .EN1(multiplexer_18_out[1]), .clk(CLK), .EN2(multiplexer_18_out[2]),
    .EN3(multiplexer_18_out[3]), .InputData(InputData), .EN16(multiplexer_18_out[16]),
    .EN17(multiplexer_18_out[17]), .EN4(multiplexer_18_out[4]), .EN5(multiplexer_18_out[5]),
    .EN6(multiplexer_18_out[6]), .EN7(multiplexer_18_out[7]), .EN18(multiplexer_18_out[18]),
    .EN19(multiplexer_18_out[19]), .EN8(multiplexer_18_out[8]), .EN9(multiplexer_18_out[9]),
    .EN20(multiplexer_18_out[20]), .EN21(multiplexer_18_out[21]), .EN10(multiplexer_18_out[10]),
    .EN11(multiplexer_18_out[11]), .EN22(multiplexer_18_out[22]), .EN23(multiplexer_18_out[23]),
    .EN12(multiplexer_18_out[12]), .EN13(multiplexer_18_out[13]), .EN24(multiplexer_18_out[24]),
    .EN25(multiplexer_18_out[25]), .EN14(multiplexer_18_out[14]), .EN15(multiplexer_18_out[15]),
    .EN26(multiplexer_18_out[26]), .EN27(multiplexer_18_out[27]), .EN28(multiplexer_18_out[28]),
    .EN29(multiplexer_18_out[29]), .EN30(multiplexer_18_out[30]), .EN31(multiplexer_18_out[31]),
    .OutputData(OutputR20));
  Register32Bit register32bit_19 (
    .EN0(multiplexer_19_out[0]), .EN1(multiplexer_19_out[1]), .clk(CLK), .EN2(multiplexer_19_out[2]),
    .EN3(multiplexer_19_out[3]), .InputData(InputData), .EN16(multiplexer_19_out[16]),
    .EN17(multiplexer_19_out[17]), .EN4(multiplexer_19_out[4]), .EN5(multiplexer_19_out[5]),
    .EN6(multiplexer_19_out[6]), .EN7(multiplexer_19_out[7]), .EN18(multiplexer_19_out[18]),
    .EN19(multiplexer_19_out[19]), .EN8(multiplexer_19_out[8]), .EN9(multiplexer_19_out[9]),
    .EN20(multiplexer_19_out[20]), .EN21(multiplexer_19_out[21]), .EN10(multiplexer_19_out[10]),
    .EN11(multiplexer_19_out[11]), .EN22(multiplexer_19_out[22]), .EN23(multiplexer_19_out[23]),
    .EN12(multiplexer_19_out[12]), .EN13(multiplexer_19_out[13]), .EN24(multiplexer_19_out[24]),
    .EN25(multiplexer_19_out[25]), .EN14(multiplexer_19_out[14]), .EN15(multiplexer_19_out[15]),
    .EN26(multiplexer_19_out[26]), .EN27(multiplexer_19_out[27]), .EN28(multiplexer_19_out[28]),
    .EN29(multiplexer_19_out[29]), .EN30(multiplexer_19_out[30]), .EN31(multiplexer_19_out[31]),
    .OutputData(OutputR24));
  Register32Bit register32bit_20 (
    .EN0(multiplexer_20_out[0]), .EN1(multiplexer_20_out[1]), .clk(CLK), .EN2(multiplexer_20_out[2]),
    .EN3(multiplexer_20_out[3]), .InputData(InputData), .EN16(multiplexer_20_out[16]),
    .EN17(multiplexer_20_out[17]), .EN4(multiplexer_20_out[4]), .EN5(multiplexer_20_out[5]),
    .EN6(multiplexer_20_out[6]), .EN7(multiplexer_20_out[7]), .EN18(multiplexer_20_out[18]),
    .EN19(multiplexer_20_out[19]), .EN8(multiplexer_20_out[8]), .EN9(multiplexer_20_out[9]),
    .EN20(multiplexer_20_out[20]), .EN21(multiplexer_20_out[21]), .EN10(multiplexer_20_out[10]),
    .EN11(multiplexer_20_out[11]), .EN22(multiplexer_20_out[22]), .EN23(multiplexer_20_out[23]),
    .EN12(multiplexer_20_out[12]), .EN13(multiplexer_20_out[13]), .EN24(multiplexer_20_out[24]),
    .EN25(multiplexer_20_out[25]), .EN14(multiplexer_20_out[14]), .EN15(multiplexer_20_out[15]),
    .EN26(multiplexer_20_out[26]), .EN27(multiplexer_20_out[27]), .EN28(multiplexer_20_out[28]),
    .EN29(multiplexer_20_out[29]), .EN30(multiplexer_20_out[30]), .EN31(multiplexer_20_out[31]),
    .OutputData(OutputR28));
  Multiplexer #(.width(32)) multiplexer_21 (
    .in0({32{ENR17AllSet}}), .in1(ENR17), .out(multiplexer_21_out), .sel(nand_27_out));
  Multiplexer #(.width(32)) multiplexer_22 (
    .in0({32{ENR21AllSet}}), .in1(ENR21), .out(multiplexer_22_out), .sel(nand_17_out));
  Multiplexer #(.width(32)) multiplexer_23 (
    .in0({32{ENR25AllSet}}), .in1(ENR25), .out(multiplexer_23_out), .sel(nand_19_out));
  Multiplexer #(.width(32)) multiplexer_24 (
    .in0({32{ENR29AllSet}}), .in1(ENR29), .out(multiplexer_24_out), .sel(nand_23_out));
  Register32Bit register32bit_21 (
    .EN0(multiplexer_21_out[0]), .EN1(multiplexer_21_out[1]), .clk(CLK), .EN2(multiplexer_21_out[2]),
    .EN3(multiplexer_21_out[3]), .InputData(InputData), .EN16(multiplexer_21_out[16]),
    .EN17(multiplexer_21_out[17]), .EN4(multiplexer_21_out[4]), .EN5(multiplexer_21_out[5]),
    .EN6(multiplexer_21_out[6]), .EN7(multiplexer_21_out[7]), .EN18(multiplexer_21_out[18]),
    .EN19(multiplexer_21_out[19]), .EN8(multiplexer_21_out[8]), .EN9(multiplexer_21_out[9]),
    .EN20(multiplexer_21_out[20]), .EN21(multiplexer_21_out[21]), .EN10(multiplexer_21_out[10]),
    .EN11(multiplexer_21_out[11]), .EN22(multiplexer_21_out[22]), .EN23(multiplexer_21_out[23]),
    .EN12(multiplexer_21_out[12]), .EN13(multiplexer_21_out[13]), .EN24(multiplexer_21_out[24]),
    .EN25(multiplexer_21_out[25]), .EN14(multiplexer_21_out[14]), .EN15(multiplexer_21_out[15]),
    .EN26(multiplexer_21_out[26]), .EN27(multiplexer_21_out[27]), .EN28(multiplexer_21_out[28]),
    .EN29(multiplexer_21_out[29]), .EN30(multiplexer_21_out[30]), .EN31(multiplexer_21_out[31]),
    .OutputData(OutputR17));
  Register32Bit register32bit_22 (
    .EN0(multiplexer_22_out[0]), .EN1(multiplexer_22_out[1]), .clk(CLK), .EN2(multiplexer_22_out[2]),
    .EN3(multiplexer_22_out[3]), .InputData(InputData), .EN16(multiplexer_22_out[16]),
    .EN17(multiplexer_22_out[17]), .EN4(multiplexer_22_out[4]), .EN5(multiplexer_22_out[5]),
    .EN6(multiplexer_22_out[6]), .EN7(multiplexer_22_out[7]), .EN18(multiplexer_22_out[18]),
    .EN19(multiplexer_22_out[19]), .EN8(multiplexer_22_out[8]), .EN9(multiplexer_22_out[9]),
    .EN20(multiplexer_22_out[20]), .EN21(multiplexer_22_out[21]), .EN10(multiplexer_22_out[10]),
    .EN11(multiplexer_22_out[11]), .EN22(multiplexer_22_out[22]), .EN23(multiplexer_22_out[23]),
    .EN12(multiplexer_22_out[12]), .EN13(multiplexer_22_out[13]), .EN24(multiplexer_22_out[24]),
    .EN25(multiplexer_22_out[25]), .EN14(multiplexer_22_out[14]), .EN15(multiplexer_22_out[15]),
    .EN26(multiplexer_22_out[26]), .EN27(multiplexer_22_out[27]), .EN28(multiplexer_22_out[28]),
    .EN29(multiplexer_22_out[29]), .EN30(multiplexer_22_out[30]), .EN31(multiplexer_22_out[31]),
    .OutputData(OutputR21));
  Register32Bit register32bit_23 (
    .EN0(multiplexer_23_out[0]), .EN1(multiplexer_23_out[1]), .clk(CLK), .EN2(multiplexer_23_out[2]),
    .EN3(multiplexer_23_out[3]), .InputData(InputData), .EN16(multiplexer_23_out[16]),
    .EN17(multiplexer_23_out[17]), .EN4(multiplexer_23_out[4]), .EN5(multiplexer_23_out[5]),
    .EN6(multiplexer_23_out[6]), .EN7(multiplexer_23_out[7]), .EN18(multiplexer_23_out[18]),
    .EN19(multiplexer_23_out[19]), .EN8(multiplexer_23_out[8]), .EN9(multiplexer_23_out[9]),
    .EN20(multiplexer_23_out[20]), .EN21(multiplexer_23_out[21]), .EN10(multiplexer_23_out[10]),
    .EN11(multiplexer_23_out[11]), .EN22(multiplexer_23_out[22]), .EN23(multiplexer_23_out[23]),
    .EN12(multiplexer_23_out[12]), .EN13(multiplexer_23_out[13]), .EN24(multiplexer_23_out[24]),
    .EN25(multiplexer_23_out[25]), .EN14(multiplexer_23_out[14]), .EN15(multiplexer_23_out[15]),
    .EN26(multiplexer_23_out[26]), .EN27(multiplexer_23_out[27]), .EN28(multiplexer_23_out[28]),
    .EN29(multiplexer_23_out[29]), .EN30(multiplexer_23_out[30]), .EN31(multiplexer_23_out[31]),
    .OutputData(OutputR25));
  Register32Bit register32bit_24 (
    .EN0(multiplexer_24_out[0]), .EN1(multiplexer_24_out[1]), .clk(CLK), .EN2(multiplexer_24_out[2]),
    .EN3(multiplexer_24_out[3]), .InputData(InputData), .EN16(multiplexer_24_out[16]),
    .EN17(multiplexer_24_out[17]), .EN4(multiplexer_24_out[4]), .EN5(multiplexer_24_out[5]),
    .EN6(multiplexer_24_out[6]), .EN7(multiplexer_24_out[7]), .EN18(multiplexer_24_out[18]),
    .EN19(multiplexer_24_out[19]), .EN8(multiplexer_24_out[8]), .EN9(multiplexer_24_out[9]),
    .EN20(multiplexer_24_out[20]), .EN21(multiplexer_24_out[21]), .EN10(multiplexer_24_out[10]),
    .EN11(multiplexer_24_out[11]), .EN22(multiplexer_24_out[22]), .EN23(multiplexer_24_out[23]),
    .EN12(multiplexer_24_out[12]), .EN13(multiplexer_24_out[13]), .EN24(multiplexer_24_out[24]),
    .EN25(multiplexer_24_out[25]), .EN14(multiplexer_24_out[14]), .EN15(multiplexer_24_out[15]),
    .EN26(multiplexer_24_out[26]), .EN27(multiplexer_24_out[27]), .EN28(multiplexer_24_out[28]),
    .EN29(multiplexer_24_out[29]), .EN30(multiplexer_24_out[30]), .EN31(multiplexer_24_out[31]),
    .OutputData(OutputR29));
  Multiplexer #(.width(32)) multiplexer_25 (
    .in0({32{ENR18AllSet}}), .in1(ENR18), .out(multiplexer_25_out), .sel(nand_28_out));
  Multiplexer #(.width(32)) multiplexer_26 (
    .in0({32{ENR22AllSet}}), .in1(ENR22), .out(multiplexer_26_out), .sel(nand_31_out));
  Multiplexer #(.width(32)) multiplexer_27 (
    .in0({32{ENR26AllSet}}), .in1(ENR26), .out(multiplexer_27_out), .sel(nand_20_out));
  Multiplexer #(.width(32)) multiplexer_28 (
    .in0({32{ENR30AllSet}}), .in1(ENR30), .out(multiplexer_28_out), .sel(nand_24_out));
  Register32Bit register32bit_25 (
    .EN0(multiplexer_25_out[0]), .EN1(multiplexer_25_out[1]), .clk(CLK), .EN2(multiplexer_25_out[2]),
    .EN3(multiplexer_25_out[3]), .InputData(InputData), .EN16(multiplexer_25_out[16]),
    .EN17(multiplexer_25_out[17]), .EN4(multiplexer_25_out[4]), .EN5(multiplexer_25_out[5]),
    .EN6(multiplexer_25_out[6]), .EN7(multiplexer_25_out[7]), .EN18(multiplexer_25_out[18]),
    .EN19(multiplexer_25_out[19]), .EN8(multiplexer_25_out[8]), .EN9(multiplexer_25_out[9]),
    .EN20(multiplexer_25_out[20]), .EN21(multiplexer_25_out[21]), .EN10(multiplexer_25_out[10]),
    .EN11(multiplexer_25_out[11]), .EN22(multiplexer_25_out[22]), .EN23(multiplexer_25_out[23]),
    .EN12(multiplexer_25_out[12]), .EN13(multiplexer_25_out[13]), .EN24(multiplexer_25_out[24]),
    .EN25(multiplexer_25_out[25]), .EN14(multiplexer_25_out[14]), .EN15(multiplexer_25_out[15]),
    .EN26(multiplexer_25_out[26]), .EN27(multiplexer_25_out[27]), .EN28(multiplexer_25_out[28]),
    .EN29(multiplexer_25_out[29]), .EN30(multiplexer_25_out[30]), .EN31(multiplexer_25_out[31]),
    .OutputData(OutputR18));
  Register32Bit register32bit_26 (
    .EN0(multiplexer_26_out[0]), .EN1(multiplexer_26_out[1]), .clk(CLK), .EN2(multiplexer_26_out[2]),
    .EN3(multiplexer_26_out[3]), .InputData(InputData), .EN16(multiplexer_26_out[16]),
    .EN17(multiplexer_26_out[17]), .EN4(multiplexer_26_out[4]), .EN5(multiplexer_26_out[5]),
    .EN6(multiplexer_26_out[6]), .EN7(multiplexer_26_out[7]), .EN18(multiplexer_26_out[18]),
    .EN19(multiplexer_26_out[19]), .EN8(multiplexer_26_out[8]), .EN9(multiplexer_26_out[9]),
    .EN20(multiplexer_26_out[20]), .EN21(multiplexer_26_out[21]), .EN10(multiplexer_26_out[10]),
    .EN11(multiplexer_26_out[11]), .EN22(multiplexer_26_out[22]), .EN23(multiplexer_26_out[23]),
    .EN12(multiplexer_26_out[12]), .EN13(multiplexer_26_out[13]), .EN24(multiplexer_26_out[24]),
    .EN25(multiplexer_26_out[25]), .EN14(multiplexer_26_out[14]), .EN15(multiplexer_26_out[15]),
    .EN26(multiplexer_26_out[26]), .EN27(multiplexer_26_out[27]), .EN28(multiplexer_26_out[28]),
    .EN29(multiplexer_26_out[29]), .EN30(multiplexer_26_out[30]), .EN31(multiplexer_26_out[31]),
    .OutputData(OutputR22));
  Register32Bit register32bit_27 (
    .EN0(multiplexer_27_out[0]), .EN1(multiplexer_27_out[1]), .clk(CLK), .EN2(multiplexer_27_out[2]),
    .EN3(multiplexer_27_out[3]), .InputData(InputData), .EN16(multiplexer_27_out[16]),
    .EN17(multiplexer_27_out[17]), .EN4(multiplexer_27_out[4]), .EN5(multiplexer_27_out[5]),
    .EN6(multiplexer_27_out[6]), .EN7(multiplexer_27_out[7]), .EN18(multiplexer_27_out[18]),
    .EN19(multiplexer_27_out[19]), .EN8(multiplexer_27_out[8]), .EN9(multiplexer_27_out[9]),
    .EN20(multiplexer_27_out[20]), .EN21(multiplexer_27_out[21]), .EN10(multiplexer_27_out[10]),
    .EN11(multiplexer_27_out[11]), .EN22(multiplexer_27_out[22]), .EN23(multiplexer_27_out[23]),
    .EN12(multiplexer_27_out[12]), .EN13(multiplexer_27_out[13]), .EN24(multiplexer_27_out[24]),
    .EN25(multiplexer_27_out[25]), .EN14(multiplexer_27_out[14]), .EN15(multiplexer_27_out[15]),
    .EN26(multiplexer_27_out[26]), .EN27(multiplexer_27_out[27]), .EN28(multiplexer_27_out[28]),
    .EN29(multiplexer_27_out[29]), .EN30(multiplexer_27_out[30]), .EN31(multiplexer_27_out[31]),
    .OutputData(OutputR26));
  Register32Bit register32bit_28 (
    .EN0(multiplexer_28_out[0]), .EN1(multiplexer_28_out[1]), .clk(CLK), .EN2(multiplexer_28_out[2]),
    .EN3(multiplexer_28_out[3]), .InputData(InputData), .EN16(multiplexer_28_out[16]),
    .EN17(multiplexer_28_out[17]), .EN4(multiplexer_28_out[4]), .EN5(multiplexer_28_out[5]),
    .EN6(multiplexer_28_out[6]), .EN7(multiplexer_28_out[7]), .EN18(multiplexer_28_out[18]),
    .EN19(multiplexer_28_out[19]), .EN8(multiplexer_28_out[8]), .EN9(multiplexer_28_out[9]),
    .EN20(multiplexer_28_out[20]), .EN21(multiplexer_28_out[21]), .EN10(multiplexer_28_out[10]),
    .EN11(multiplexer_28_out[11]), .EN22(multiplexer_28_out[22]), .EN23(multiplexer_28_out[23]),
    .EN12(multiplexer_28_out[12]), .EN13(multiplexer_28_out[13]), .EN24(multiplexer_28_out[24]),
    .EN25(multiplexer_28_out[25]), .EN14(multiplexer_28_out[14]), .EN15(multiplexer_28_out[15]),
    .EN26(multiplexer_28_out[26]), .EN27(multiplexer_28_out[27]), .EN28(multiplexer_28_out[28]),
    .EN29(multiplexer_28_out[29]), .EN30(multiplexer_28_out[30]), .EN31(multiplexer_28_out[31]),
    .OutputData(OutputR30));
  Multiplexer #(.width(32)) multiplexer_29 (
    .in0({32{ENR19AllSet}}), .in1(ENR19), .out(multiplexer_29_out), .sel(nand_29_out));
  Multiplexer #(.width(32)) multiplexer_30 (
    .in0({32{ENR23AllSet}}), .in1(ENR23), .out(multiplexer_30_out), .sel(nand_32_out));
  Multiplexer #(.width(32)) multiplexer_31 (
    .in0({32{ENR27AllSet}}), .in1(ENR27), .out(multiplexer_31_out), .sel(nand_21_out));
  Multiplexer #(.width(32)) multiplexer_32 (
    .in0({32{ENR31AllSet}}), .in1(ENR31), .out(multiplexer_32_out), .sel(nand_25_out));
  Register32Bit register32bit_29 (
    .EN0(multiplexer_29_out[0]), .EN1(multiplexer_29_out[1]), .clk(CLK), .EN2(multiplexer_29_out[2]),
    .EN3(multiplexer_29_out[3]), .InputData(InputData), .EN16(multiplexer_29_out[16]),
    .EN17(multiplexer_29_out[17]), .EN4(multiplexer_29_out[4]), .EN5(multiplexer_29_out[5]),
    .EN6(multiplexer_29_out[6]), .EN7(multiplexer_29_out[7]), .EN18(multiplexer_29_out[18]),
    .EN19(multiplexer_29_out[19]), .EN8(multiplexer_29_out[8]), .EN9(multiplexer_29_out[9]),
    .EN20(multiplexer_29_out[20]), .EN21(multiplexer_29_out[21]), .EN10(multiplexer_29_out[10]),
    .EN11(multiplexer_29_out[11]), .EN22(multiplexer_29_out[22]), .EN23(multiplexer_29_out[23]),
    .EN12(multiplexer_29_out[12]), .EN13(multiplexer_29_out[13]), .EN24(multiplexer_29_out[24]),
    .EN25(multiplexer_29_out[25]), .EN14(multiplexer_29_out[14]), .EN15(multiplexer_29_out[15]),
    .EN26(multiplexer_29_out[26]), .EN27(multiplexer_29_out[27]), .EN28(multiplexer_29_out[28]),
    .EN29(multiplexer_29_out[29]), .EN30(multiplexer_29_out[30]), .EN31(multiplexer_29_out[31]),
    .OutputData(OutputR19));
  Register32Bit register32bit_30 (
    .EN0(multiplexer_30_out[0]), .EN1(multiplexer_30_out[1]), .clk(CLK), .EN2(multiplexer_30_out[2]),
    .EN3(multiplexer_30_out[3]), .InputData(InputData), .EN16(multiplexer_30_out[16]),
    .EN17(multiplexer_30_out[17]), .EN4(multiplexer_30_out[4]), .EN5(multiplexer_30_out[5]),
    .EN6(multiplexer_30_out[6]), .EN7(multiplexer_30_out[7]), .EN18(multiplexer_30_out[18]),
    .EN19(multiplexer_30_out[19]), .EN8(multiplexer_30_out[8]), .EN9(multiplexer_30_out[9]),
    .EN20(multiplexer_30_out[20]), .EN21(multiplexer_30_out[21]), .EN10(multiplexer_30_out[10]),
    .EN11(multiplexer_30_out[11]), .EN22(multiplexer_30_out[22]), .EN23(multiplexer_30_out[23]),
    .EN12(multiplexer_30_out[12]), .EN13(multiplexer_30_out[13]), .EN24(multiplexer_30_out[24]),
    .EN25(multiplexer_30_out[25]), .EN14(multiplexer_30_out[14]), .EN15(multiplexer_30_out[15]),
    .EN26(multiplexer_30_out[26]), .EN27(multiplexer_30_out[27]), .EN28(multiplexer_30_out[28]),
    .EN29(multiplexer_30_out[29]), .EN30(multiplexer_30_out[30]), .EN31(multiplexer_30_out[31]),
    .OutputData(OutputR23));
  Register32Bit register32bit_31 (
    .EN0(multiplexer_31_out[0]), .EN1(multiplexer_31_out[1]), .clk(CLK), .EN2(multiplexer_31_out[2]),
    .EN3(multiplexer_31_out[3]), .InputData(InputData), .EN16(multiplexer_31_out[16]),
    .EN17(multiplexer_31_out[17]), .EN4(multiplexer_31_out[4]), .EN5(multiplexer_31_out[5]),
    .EN6(multiplexer_31_out[6]), .EN7(multiplexer_31_out[7]), .EN18(multiplexer_31_out[18]),
    .EN19(multiplexer_31_out[19]), .EN8(multiplexer_31_out[8]), .EN9(multiplexer_31_out[9]),
    .EN20(multiplexer_31_out[20]), .EN21(multiplexer_31_out[21]), .EN10(multiplexer_31_out[10]),
    .EN11(multiplexer_31_out[11]), .EN22(multiplexer_31_out[22]), .EN23(multiplexer_31_out[23]),
    .EN12(multiplexer_31_out[12]), .EN13(multiplexer_31_out[13]), .EN24(multiplexer_31_out[24]),
    .EN25(multiplexer_31_out[25]), .EN14(multiplexer_31_out[14]), .EN15(multiplexer_31_out[15]),
    .EN26(multiplexer_31_out[26]), .EN27(multiplexer_31_out[27]), .EN28(multiplexer_31_out[28]),
    .EN29(multiplexer_31_out[29]), .EN30(multiplexer_31_out[30]), .EN31(multiplexer_31_out[31]),
    .OutputData(OutputR27));
  Register32Bit register32bit_32 (
    .EN0(multiplexer_32_out[0]), .EN1(multiplexer_32_out[1]), .clk(CLK), .EN2(multiplexer_32_out[2]),
    .EN3(multiplexer_32_out[3]), .InputData(InputData), .EN16(multiplexer_32_out[16]),
    .EN17(multiplexer_32_out[17]), .EN4(multiplexer_32_out[4]), .EN5(multiplexer_32_out[5]),
    .EN6(multiplexer_32_out[6]), .EN7(multiplexer_32_out[7]), .EN18(multiplexer_32_out[18]),
    .EN19(multiplexer_32_out[19]), .EN8(multiplexer_32_out[8]), .EN9(multiplexer_32_out[9]),
    .EN20(multiplexer_32_out[20]), .EN21(multiplexer_32_out[21]), .EN10(multiplexer_32_out[10]),
    .EN11(multiplexer_32_out[11]), .EN22(multiplexer_32_out[22]), .EN23(multiplexer_32_out[23]),
    .EN12(multiplexer_32_out[12]), .EN13(multiplexer_32_out[13]), .EN24(multiplexer_32_out[24]),
    .EN25(multiplexer_32_out[25]), .EN14(multiplexer_32_out[14]), .EN15(multiplexer_32_out[15]),
    .EN26(multiplexer_32_out[26]), .EN27(multiplexer_32_out[27]), .EN28(multiplexer_32_out[28]),
    .EN29(multiplexer_32_out[29]), .EN30(multiplexer_32_out[30]), .EN31(multiplexer_32_out[31]),
    .OutputData(OutputR31));
  not not_17 (not_17_out, SelectionR24);
  not not_18 (not_18_out, SelectionR25);
  not not_19 (not_19_out, SelectionR26);
  not not_20 (not_20_out, SelectionR27);
  not not_21 (not_21_out, SelectionR28);
  xor xor_17 (xor_17_out, ENR29AllSet, SelectionR29);
  not not_22 (not_22_out, SelectionR29);
  not not_23 (not_23_out, SelectionR30);
  not not_24 (not_24_out, SelectionR31);
  not not_25 (not_25_out, SelectionR16);
  xor xor_18 (xor_18_out, ENR17AllSet, SelectionR17);
  not not_26 (not_26_out, SelectionR17);
  not not_27 (not_27_out, SelectionR18);
  not not_28 (not_28_out, SelectionR19);
  xor xor_19 (xor_19_out, ENR20AllSet, SelectionR20);
  not not_29 (not_29_out, SelectionR20);
  xor xor_20 (xor_20_out, ENR21AllSet, SelectionR21);
  not not_30 (not_30_out, SelectionR21);
  xor xor_21 (xor_21_out, ENR22AllSet, SelectionR22);
  not not_31 (not_31_out, SelectionR22);
  xor xor_22 (xor_22_out, ENR23AllSet, SelectionR23);
  not not_32 (not_32_out, SelectionR23);
  xor xor_23 (xor_23_out, ENR24AllSet, SelectionR24);
  xor xor_24 (xor_24_out, ENR25AllSet, SelectionR25);
  xor xor_25 (xor_25_out, ENR26AllSet, SelectionR26);
  xor xor_26 (xor_26_out, ENR27AllSet, SelectionR27);
  xor xor_27 (xor_27_out, ENR28AllSet, SelectionR28);
  xor xor_28 (xor_28_out, ENR30AllSet, SelectionR30);
  xor xor_29 (xor_29_out, ENR31AllSet, SelectionR31);
  xor xor_30 (xor_30_out, ENR16AllSet, SelectionR16);
  xor xor_31 (xor_31_out, ENR18AllSet, SelectionR18);
  xor xor_32 (xor_32_out, ENR19AllSet, SelectionR19);
  nand nand_17 (nand_17_out, xor_20_out, not_30_out);
  nand nand_18 (nand_18_out, xor_23_out, not_17_out);
  nand nand_19 (nand_19_out, xor_24_out, not_18_out);
  nand nand_20 (nand_20_out, xor_25_out, not_19_out);
  nand nand_21 (nand_21_out, xor_26_out, not_20_out);
  nand nand_22 (nand_22_out, xor_27_out, not_21_out);
  nand nand_23 (nand_23_out, xor_17_out, not_22_out);
  nand nand_24 (nand_24_out, xor_28_out, not_23_out);
  nand nand_25 (nand_25_out, xor_29_out, not_24_out);
  nand nand_26 (nand_26_out, xor_30_out, not_25_out);
  nand nand_27 (nand_27_out, xor_18_out, not_26_out);
  nand nand_28 (nand_28_out, xor_31_out, not_27_out);
  nand nand_29 (nand_29_out, xor_32_out, not_28_out);
  nand nand_30 (nand_30_out, xor_19_out, not_29_out);
  nand nand_31 (nand_31_out, xor_21_out, not_31_out);
  nand nand_32 (nand_32_out, xor_22_out, not_32_out);

  // Notes on the sheet:
  //   32 Registers File
  //   32 Registers File
  //   32 Registers File
  //   32 Registers File
  //   32 Registers File
  //   32 Registers File
  //   32 Registers File
  //   32 Registers File
endmodule

module smallstuff (
  input  selectionIN,
  input  [31:0] BitIN,
  output [31:0] out_3
);

  assign out_3 = {32{selectionIN}} & BitIN;  // AND_Gate and_1, 32 bits wide
endmodule
module copypasteregisterfile (
  input  [31:0] BitPicking,
  input  [4:0] DECODER_INPUT_ADDRESSING_AllSets,
  input  [31:0] Main_INPUT,
  input  ENforALLSet,
  input  R0Selection,
  input  CLK,
  input  R1Selection,
  input  R2Selection,
  input  R16Selection,
  input  R3Selection,
  input  R17Selection,
  input  R18Selection,
  input  [4:0] READ1_SELECT,
  input  R19Selection,
  input  R4Selection,
  input  R5Selection,
  input  R20Selection,
  input  R6Selection,
  input  R21Selection,
  input  R7Selection,
  input  R22Selection,
  input  [4:0] READ2_SELECT,
  input  R23Selection,
  input  R8Selection,
  input  R9Selection,
  input  R24Selection,
  input  R10Selection,
  input  R25Selection,
  input  R11Selection,
  input  R26Selection,
  input  R27Selection,
  input  R12Selection,
  input  R13Selection,
  input  R28Selection,
  input  R14Selection,
  input  R29Selection,
  input  R15Selection,
  input  R30Selection,
  input  R31Selection,
  output [31:0] READ1_OUTPUT,
  output [31:0] READ2_OUTPUT
);

  wire and_1_out, and_2_out, and_3_out, and_4_out, and_5_out, and_6_out, and_7_out, and_8_out, and_9_out,
       and_10_out, and_11_out, and_12_out, and_13_out, and_14_out, and_15_out, and_16_out, and_17_out,
       and_18_out, and_19_out, and_20_out, and_21_out, and_22_out, and_23_out, and_24_out, and_25_out,
       and_26_out, and_27_out, and_28_out, and_29_out, and_30_out, and_31_out, and_32_out, B00000_out,
       B00001_out, B00010_out, B00011_out, B00100_out, B00101_out, B00110_out, B00111_out, B01000_out,
       B01001_out, B01010_out, B01011_out, B01100_out, B01101_out, B01110_out, B01111_out, B10000_out,
       B10001_out, B10010_out, B10011_out, B10100_out, B10101_out, B10110_out, B10111_out, B11000_out,
       B11001_out, B11010_out, B11011_out, B11100_out, B11101_out, B11110_out, B11111_out, not_1_out,
       not_2_out, not_3_out, not_4_out, not_5_out;
  wire [31:0] registers32_1_outputr0, registers32_1_outputr1, registers32_1_outputr2, registers32_1_outputr3,
       registers32_1_outputr4, registers32_1_outputr5, registers32_1_outputr6, registers32_1_outputr7,
       registers32_1_outputr8, registers32_1_outputr9, registers32_1_outputr10, registers32_1_outputr11,
       registers32_1_outputr12, registers32_1_outputr13, registers32_1_outputr14, registers32_1_outputr15,
       registers32_1_outputr16, registers32_1_outputr17, registers32_1_outputr18, registers32_1_outputr19,
       registers32_1_outputr20, registers32_1_outputr21, registers32_1_outputr22, registers32_1_outputr23,
       registers32_1_outputr24, registers32_1_outputr25, registers32_1_outputr26, registers32_1_outputr27,
       registers32_1_outputr28, registers32_1_outputr29, registers32_1_outputr30, registers32_1_outputr31,
       smallstuff_1_out_3, smallstuff_2_out_3, smallstuff_3_out_3, smallstuff_4_out_3, smallstuff_5_out_3,
       smallstuff_6_out_3, smallstuff_7_out_3, smallstuff_8_out_3, smallstuff_9_out_3, smallstuff_10_out_3,
       smallstuff_11_out_3, smallstuff_12_out_3, smallstuff_13_out_3, smallstuff_14_out_3,
       smallstuff_15_out_3, smallstuff_16_out_3, smallstuff_17_out_3, smallstuff_18_out_3,
       smallstuff_19_out_3, smallstuff_20_out_3, smallstuff_21_out_3, smallstuff_22_out_3,
       smallstuff_23_out_3, smallstuff_24_out_3, smallstuff_25_out_3, smallstuff_26_out_3,
       smallstuff_27_out_3, smallstuff_28_out_3, smallstuff_29_out_3, smallstuff_30_out_3,
       smallstuff_31_out_3, smallstuff_32_out_3;

  not not_1 (not_1_out, DECODER_INPUT_ADDRESSING_AllSets[4]);
  not not_2 (not_2_out, DECODER_INPUT_ADDRESSING_AllSets[3]);
  not not_3 (not_3_out, DECODER_INPUT_ADDRESSING_AllSets[2]);
  not not_4 (not_4_out, DECODER_INPUT_ADDRESSING_AllSets[1]);
  not not_5 (not_5_out, DECODER_INPUT_ADDRESSING_AllSets[0]);
  and B00000 (B00000_out, not_5_out, not_4_out, not_3_out, not_2_out, not_1_out);
  and B00001 (B00001_out, DECODER_INPUT_ADDRESSING_AllSets[0], not_4_out, not_3_out, not_2_out, not_1_out);
  and B00010 (B00010_out, not_5_out, DECODER_INPUT_ADDRESSING_AllSets[1], not_3_out, not_2_out, not_1_out);
  and B00011 (B00011_out, DECODER_INPUT_ADDRESSING_AllSets[0], DECODER_INPUT_ADDRESSING_AllSets[1], not_3_out, not_2_out, not_1_out);
  and B00100 (B00100_out, not_5_out, not_4_out, DECODER_INPUT_ADDRESSING_AllSets[2], not_2_out, not_1_out);
  and B00101 (B00101_out, DECODER_INPUT_ADDRESSING_AllSets[0], not_4_out, DECODER_INPUT_ADDRESSING_AllSets[2], not_2_out, not_1_out);
  and B00110 (B00110_out, not_5_out, DECODER_INPUT_ADDRESSING_AllSets[1], DECODER_INPUT_ADDRESSING_AllSets[2], not_2_out, not_1_out);
  and B00111 (B00111_out, DECODER_INPUT_ADDRESSING_AllSets[0], DECODER_INPUT_ADDRESSING_AllSets[1], DECODER_INPUT_ADDRESSING_AllSets[2], not_2_out, not_1_out);
  and B01000 (B01000_out, not_5_out, not_4_out, not_3_out, DECODER_INPUT_ADDRESSING_AllSets[3], not_1_out);
  and B01001 (B01001_out, DECODER_INPUT_ADDRESSING_AllSets[0], not_4_out, not_3_out, DECODER_INPUT_ADDRESSING_AllSets[3], not_1_out);
  and B01010 (B01010_out, not_5_out, DECODER_INPUT_ADDRESSING_AllSets[1], not_3_out, DECODER_INPUT_ADDRESSING_AllSets[3], not_1_out);
  and B01011 (B01011_out, DECODER_INPUT_ADDRESSING_AllSets[0], DECODER_INPUT_ADDRESSING_AllSets[1], not_3_out, DECODER_INPUT_ADDRESSING_AllSets[3], not_1_out);
  and B01100 (B01100_out, not_5_out, not_4_out, DECODER_INPUT_ADDRESSING_AllSets[2], DECODER_INPUT_ADDRESSING_AllSets[3], not_1_out);
  and B01101 (B01101_out, DECODER_INPUT_ADDRESSING_AllSets[0], not_4_out, DECODER_INPUT_ADDRESSING_AllSets[2], DECODER_INPUT_ADDRESSING_AllSets[3], not_1_out);
  and B01110 (B01110_out, not_5_out, DECODER_INPUT_ADDRESSING_AllSets[1], DECODER_INPUT_ADDRESSING_AllSets[2], DECODER_INPUT_ADDRESSING_AllSets[3], not_1_out);
  and B01111 (B01111_out, DECODER_INPUT_ADDRESSING_AllSets[0], DECODER_INPUT_ADDRESSING_AllSets[1], DECODER_INPUT_ADDRESSING_AllSets[2], DECODER_INPUT_ADDRESSING_AllSets[3], not_1_out);
  and B10000 (B10000_out, not_5_out, not_4_out, not_3_out, not_2_out, DECODER_INPUT_ADDRESSING_AllSets[4]);
  and B10001 (B10001_out, DECODER_INPUT_ADDRESSING_AllSets[0], not_4_out, not_3_out, not_2_out, DECODER_INPUT_ADDRESSING_AllSets[4]);
  and B10010 (B10010_out, not_5_out, DECODER_INPUT_ADDRESSING_AllSets[1], not_3_out, not_2_out, DECODER_INPUT_ADDRESSING_AllSets[4]);
  and B10011 (B10011_out, DECODER_INPUT_ADDRESSING_AllSets[0], DECODER_INPUT_ADDRESSING_AllSets[1], not_3_out, not_2_out, DECODER_INPUT_ADDRESSING_AllSets[4]);
  and B10100 (B10100_out, not_5_out, not_4_out, DECODER_INPUT_ADDRESSING_AllSets[2], not_2_out, DECODER_INPUT_ADDRESSING_AllSets[4]);
  and B10101 (B10101_out, DECODER_INPUT_ADDRESSING_AllSets[0], not_4_out, DECODER_INPUT_ADDRESSING_AllSets[2], not_2_out, DECODER_INPUT_ADDRESSING_AllSets[4]);
  and B10110 (B10110_out, not_5_out, DECODER_INPUT_ADDRESSING_AllSets[1], DECODER_INPUT_ADDRESSING_AllSets[2], not_2_out, DECODER_INPUT_ADDRESSING_AllSets[4]);
  and B10111 (B10111_out, DECODER_INPUT_ADDRESSING_AllSets[0], DECODER_INPUT_ADDRESSING_AllSets[1], DECODER_INPUT_ADDRESSING_AllSets[2], not_2_out, DECODER_INPUT_ADDRESSING_AllSets[4]);
  and B11000 (B11000_out, not_5_out, not_4_out, not_3_out, DECODER_INPUT_ADDRESSING_AllSets[3], DECODER_INPUT_ADDRESSING_AllSets[4]);
  and B11001 (B11001_out, DECODER_INPUT_ADDRESSING_AllSets[0], not_4_out, not_3_out, DECODER_INPUT_ADDRESSING_AllSets[3], DECODER_INPUT_ADDRESSING_AllSets[4]);
  and B11010 (B11010_out, not_5_out, DECODER_INPUT_ADDRESSING_AllSets[1], not_3_out, DECODER_INPUT_ADDRESSING_AllSets[3], DECODER_INPUT_ADDRESSING_AllSets[4]);
  and B11011 (B11011_out, DECODER_INPUT_ADDRESSING_AllSets[0], DECODER_INPUT_ADDRESSING_AllSets[1], not_3_out, DECODER_INPUT_ADDRESSING_AllSets[3], DECODER_INPUT_ADDRESSING_AllSets[4]);
  and B11100 (B11100_out, not_5_out, not_4_out, DECODER_INPUT_ADDRESSING_AllSets[2], DECODER_INPUT_ADDRESSING_AllSets[3], DECODER_INPUT_ADDRESSING_AllSets[4]);
  and B11101 (B11101_out, DECODER_INPUT_ADDRESSING_AllSets[0], not_4_out, DECODER_INPUT_ADDRESSING_AllSets[2], DECODER_INPUT_ADDRESSING_AllSets[3], DECODER_INPUT_ADDRESSING_AllSets[4]);
  and B11110 (B11110_out, not_5_out, DECODER_INPUT_ADDRESSING_AllSets[1], DECODER_INPUT_ADDRESSING_AllSets[2], DECODER_INPUT_ADDRESSING_AllSets[3], DECODER_INPUT_ADDRESSING_AllSets[4]);
  and B11111 (B11111_out, DECODER_INPUT_ADDRESSING_AllSets[0], DECODER_INPUT_ADDRESSING_AllSets[1], DECODER_INPUT_ADDRESSING_AllSets[2], DECODER_INPUT_ADDRESSING_AllSets[3], DECODER_INPUT_ADDRESSING_AllSets[4]);
  and and_1 (and_1_out, ENforALLSet, B00000_out);
  and and_2 (and_2_out, ENforALLSet, B00001_out);
  and and_3 (and_3_out, ENforALLSet, B00010_out);
  and and_4 (and_4_out, ENforALLSet, B00011_out);
  and and_5 (and_5_out, ENforALLSet, B00100_out);
  and and_6 (and_6_out, ENforALLSet, B00101_out);
  and and_7 (and_7_out, ENforALLSet, B00110_out);
  and and_8 (and_8_out, ENforALLSet, B00111_out);
  and and_9 (and_9_out, ENforALLSet, B01000_out);
  and and_10 (and_10_out, ENforALLSet, B01001_out);
  and and_11 (and_11_out, ENforALLSet, B01010_out);
  and and_12 (and_12_out, ENforALLSet, B01011_out);
  and and_13 (and_13_out, ENforALLSet, B01100_out);
  and and_14 (and_14_out, ENforALLSet, B01101_out);
  and and_15 (and_15_out, ENforALLSet, B01110_out);
  and and_16 (and_16_out, ENforALLSet, B01111_out);
  and and_17 (and_17_out, ENforALLSet, B10000_out);
  and and_18 (and_18_out, ENforALLSet, B10001_out);
  and and_19 (and_19_out, ENforALLSet, B10010_out);
  and and_20 (and_20_out, ENforALLSet, B10011_out);
  and and_21 (and_21_out, ENforALLSet, B10100_out);
  and and_22 (and_22_out, ENforALLSet, B10101_out);
  and and_23 (and_23_out, ENforALLSet, B10110_out);
  and and_24 (and_24_out, ENforALLSet, B10111_out);
  and and_25 (and_25_out, ENforALLSet, B11000_out);
  and and_26 (and_26_out, ENforALLSet, B11001_out);
  and and_27 (and_27_out, ENforALLSet, B11010_out);
  and and_28 (and_28_out, ENforALLSet, B11011_out);
  and and_29 (and_29_out, ENforALLSet, B11100_out);
  and and_30 (and_30_out, ENforALLSet, B11101_out);
  and and_31 (and_31_out, ENforALLSet, B11110_out);
  and and_32 (and_32_out, ENforALLSet, B11111_out);
  smallstuff smallstuff_1 (.selectionIN(R21Selection), .BitIN(BitPicking), .out_3(smallstuff_1_out_3));
  smallstuff smallstuff_2 (.selectionIN(R22Selection), .BitIN(BitPicking), .out_3(smallstuff_2_out_3));
  smallstuff smallstuff_3 (.selectionIN(R23Selection), .BitIN(BitPicking), .out_3(smallstuff_3_out_3));
  smallstuff smallstuff_4 (.selectionIN(R7Selection), .BitIN(BitPicking), .out_3(smallstuff_4_out_3));
  smallstuff smallstuff_5 (.selectionIN(R8Selection), .BitIN(BitPicking), .out_3(smallstuff_5_out_3));
  smallstuff smallstuff_6 (.selectionIN(R13Selection), .BitIN(BitPicking), .out_3(smallstuff_6_out_3));
  smallstuff smallstuff_7 (.selectionIN(R14Selection), .BitIN(BitPicking), .out_3(smallstuff_7_out_3));
  smallstuff smallstuff_8 (.selectionIN(R0Selection), .BitIN(BitPicking), .out_3(smallstuff_8_out_3));
  smallstuff smallstuff_9 (.selectionIN(R2Selection), .BitIN(BitPicking), .out_3(smallstuff_9_out_3));
  smallstuff smallstuff_10 (.selectionIN(R9Selection), .BitIN(BitPicking), .out_3(smallstuff_10_out_3));
  smallstuff smallstuff_11 (.selectionIN(R10Selection), .BitIN(BitPicking), .out_3(smallstuff_11_out_3));
  smallstuff smallstuff_12 (.selectionIN(R15Selection), .BitIN(BitPicking), .out_3(smallstuff_12_out_3));
  smallstuff smallstuff_13 (.selectionIN(R16Selection), .BitIN(BitPicking), .out_3(smallstuff_13_out_3));
  smallstuff smallstuff_14 (.selectionIN(R24Selection), .BitIN(BitPicking), .out_3(smallstuff_14_out_3));
  smallstuff smallstuff_15 (.selectionIN(R25Selection), .BitIN(BitPicking), .out_3(smallstuff_15_out_3));
  smallstuff smallstuff_16 (.selectionIN(R26Selection), .BitIN(BitPicking), .out_3(smallstuff_16_out_3));
  smallstuff smallstuff_17 (.selectionIN(R1Selection), .BitIN(BitPicking), .out_3(smallstuff_17_out_3));
  smallstuff smallstuff_18 (.selectionIN(R3Selection), .BitIN(BitPicking), .out_3(smallstuff_18_out_3));
  smallstuff smallstuff_19 (.selectionIN(R11Selection), .BitIN(BitPicking), .out_3(smallstuff_19_out_3));
  smallstuff smallstuff_20 (.selectionIN(R17Selection), .BitIN(BitPicking), .out_3(smallstuff_20_out_3));
  smallstuff smallstuff_21 (.selectionIN(R18Selection), .BitIN(BitPicking), .out_3(smallstuff_21_out_3));
  smallstuff smallstuff_22 (.selectionIN(R27Selection), .BitIN(BitPicking), .out_3(smallstuff_22_out_3));
  smallstuff smallstuff_23 (.selectionIN(R28Selection), .BitIN(BitPicking), .out_3(smallstuff_23_out_3));
  smallstuff smallstuff_24 (.selectionIN(R29Selection), .BitIN(BitPicking), .out_3(smallstuff_24_out_3));
  smallstuff smallstuff_25 (.selectionIN(R4Selection), .BitIN(BitPicking), .out_3(smallstuff_25_out_3));
  smallstuff smallstuff_26 (.selectionIN(R5Selection), .BitIN(BitPicking), .out_3(smallstuff_26_out_3));
  smallstuff smallstuff_27 (.selectionIN(R30Selection), .BitIN(BitPicking), .out_3(smallstuff_27_out_3));
  smallstuff smallstuff_28 (.selectionIN(R31Selection), .BitIN(BitPicking), .out_3(smallstuff_28_out_3));
  smallstuff smallstuff_29 (.selectionIN(R12Selection), .BitIN(BitPicking), .out_3(smallstuff_29_out_3));
  smallstuff smallstuff_30 (.selectionIN(R19Selection), .BitIN(BitPicking), .out_3(smallstuff_30_out_3));
  smallstuff smallstuff_31 (.selectionIN(R20Selection), .BitIN(BitPicking), .out_3(smallstuff_31_out_3));
  smallstuff smallstuff_32 (.selectionIN(R6Selection), .BitIN(BitPicking), .out_3(smallstuff_32_out_3));
  Registers32 registers32_1 (
    .ENR0AllSet(and_1_out), .SelectionR0(R0Selection), .InputData(Main_INPUT), .CLK(CLK),
    .ENR1AllSet(and_2_out), .SelectionR1(R1Selection), .ENR2AllSet(and_3_out), .SelectionR2(R2Selection),
    .ENR16AllSet(and_17_out), .SelectionR16(R16Selection), .ENR3AllSet3(and_4_out),
    .SelectionR3(R3Selection), .ENR17AllSet(and_18_out), .SelectionR17(R17Selection),
    .ENR18AllSet(and_19_out), .SelectionR18(R18Selection), .ENR19AllSet(and_20_out),
    .ENR0(smallstuff_8_out_3), .ENR1(smallstuff_17_out_3), .ENR2(smallstuff_9_out_3),
    .ENR3(smallstuff_18_out_3), .ENR16(smallstuff_13_out_3), .ENR17(smallstuff_20_out_3),
    .ENR18(smallstuff_21_out_3), .ENR19(smallstuff_30_out_3), .SelectionR19(R19Selection),
    .ENR4AllSet(and_5_out), .SelectionR4(R4Selection), .ENR5AllSet(and_6_out), .SelectionR5(R5Selection),
    .ENR20AllSet(and_21_out), .SelectionR20(R20Selection), .ENR6AllSet(and_7_out), .SelectionR6(R6Selection),
    .ENR21AllSet(and_22_out), .SelectionR21(R21Selection), .ENR7AllSet(and_8_out), .SelectionR7(R7Selection),
    .ENR22AllSet(and_23_out), .SelectionR22(R22Selection), .ENR23AllSet(and_24_out),
    .ENR4(smallstuff_25_out_3), .ENR5(smallstuff_26_out_3), .ENR6(smallstuff_32_out_3),
    .ENR7(smallstuff_4_out_3), .ENR20(smallstuff_31_out_3), .ENR21(smallstuff_1_out_3),
    .ENR22(smallstuff_2_out_3), .ENR23(smallstuff_3_out_3), .SelectionR23(R23Selection),
    .ENR8AllSet(and_9_out), .SelectionR8(R8Selection), .ENR9AllSet(and_10_out), .ENR24AllSet(and_25_out),
    .SelectionR9(R9Selection), .SelectionR24(R24Selection), .ENR10AllSet(and_11_out),
    .ENR25AllSet(and_26_out), .SelectionR10(R10Selection), .SelectionR25(R25Selection),
    .ENR11AllSet(and_12_out), .SelectionR11(R11Selection), .ENR26AllSet(and_27_out),
    .SelectionR26(R26Selection), .ENR27AllSet(and_28_out), .ENR8(smallstuff_5_out_3),
    .ENR9(smallstuff_10_out_3), .ENR10(smallstuff_11_out_3), .ENR11(smallstuff_19_out_3),
    .ENR24(smallstuff_14_out_3), .ENR25(smallstuff_15_out_3), .ENR26(smallstuff_16_out_3),
    .ENR27(smallstuff_22_out_3), .SelectionR27(R27Selection), .ENR12AllSet(and_13_out),
    .SelectionR12(R12Selection), .ENR13AllSet(and_14_out), .SelectionR13(R13Selection),
    .ENR28AllSet(and_29_out), .SelectionR28(R28Selection), .ENR14AllSet(and_15_out),
    .SelectionR14(R14Selection), .ENR29AllSet(and_30_out), .SelectionR29(R29Selection),
    .ENR15AllSet(and_16_out), .SelectionR15(R15Selection), .ENR30AllSet(and_31_out),
    .SelectionR30(R30Selection), .ENR31AllSet(and_32_out), .ENR12(smallstuff_29_out_3),
    .ENR13(smallstuff_6_out_3), .ENR14(smallstuff_7_out_3), .ENR15(smallstuff_12_out_3),
    .ENR28(smallstuff_23_out_3), .ENR29(smallstuff_24_out_3), .ENR30(smallstuff_27_out_3),
    .ENR31(smallstuff_28_out_3), .SelectionR31(R31Selection), .OutputR0(registers32_1_outputr0),
    .OutputR1(registers32_1_outputr1), .OutputR2(registers32_1_outputr2), .OutputR3(registers32_1_outputr3),
    .OutputR16(registers32_1_outputr16), .OutputR17(registers32_1_outputr17),
    .OutputR18(registers32_1_outputr18), .OutputR19(registers32_1_outputr19),
    .OutputR4(registers32_1_outputr4), .OutputR5(registers32_1_outputr5), .OutputR6(registers32_1_outputr6),
    .OutputR7(registers32_1_outputr7), .OutputR20(registers32_1_outputr20),
    .OutputR21(registers32_1_outputr21), .OutputR22(registers32_1_outputr22),
    .OutputR23(registers32_1_outputr23), .OutputR8(registers32_1_outputr8),
    .OutputR9(registers32_1_outputr9), .OutputR10(registers32_1_outputr10),
    .OutputR11(registers32_1_outputr11), .OutputR24(registers32_1_outputr24),
    .OutputR25(registers32_1_outputr25), .OutputR26(registers32_1_outputr26),
    .OutputR27(registers32_1_outputr27), .OutputR12(registers32_1_outputr12),
    .OutputR13(registers32_1_outputr13), .OutputR14(registers32_1_outputr14),
    .OutputR15(registers32_1_outputr15), .OutputR28(registers32_1_outputr28),
    .OutputR29(registers32_1_outputr29), .OutputR30(registers32_1_outputr30),
    .OutputR31(registers32_1_outputr31));
  Multiplexer #(.select(5), .width(32)) multiplexer_1 (
    .in0(registers32_1_outputr0), .in1(registers32_1_outputr1), .in2(registers32_1_outputr2),
    .in3(registers32_1_outputr3), .in4(registers32_1_outputr4), .in5(registers32_1_outputr5),
    .in6(registers32_1_outputr6), .in7(registers32_1_outputr7), .in8(registers32_1_outputr8),
    .in9(registers32_1_outputr9), .in10(registers32_1_outputr10), .in11(registers32_1_outputr11),
    .in12(registers32_1_outputr12), .in13(registers32_1_outputr13), .in14(registers32_1_outputr14),
    .in15(registers32_1_outputr15), .in16(registers32_1_outputr16), .in17(registers32_1_outputr17),
    .in18(registers32_1_outputr18), .in19(registers32_1_outputr19), .in20(registers32_1_outputr20),
    .in21(registers32_1_outputr21), .in22(registers32_1_outputr22), .in23(registers32_1_outputr23),
    .in24(registers32_1_outputr24), .in25(registers32_1_outputr25), .in26(registers32_1_outputr26),
    .in27(registers32_1_outputr27), .in28(registers32_1_outputr28), .in29(registers32_1_outputr29),
    .in30(registers32_1_outputr30), .in31(registers32_1_outputr31), .out(READ1_OUTPUT), .sel(READ1_SELECT));
  Multiplexer #(.select(5), .width(32)) multiplexer_2 (
    .in0(registers32_1_outputr0), .in1(registers32_1_outputr1), .in2(registers32_1_outputr2),
    .in3(registers32_1_outputr3), .in4(registers32_1_outputr4), .in5(registers32_1_outputr5),
    .in6(registers32_1_outputr6), .in7(registers32_1_outputr7), .in8(registers32_1_outputr8),
    .in9(registers32_1_outputr9), .in10(registers32_1_outputr10), .in11(registers32_1_outputr11),
    .in12(registers32_1_outputr12), .in13(registers32_1_outputr13), .in14(registers32_1_outputr14),
    .in15(registers32_1_outputr15), .in16(registers32_1_outputr16), .in17(registers32_1_outputr17),
    .in18(registers32_1_outputr18), .in19(registers32_1_outputr19), .in20(registers32_1_outputr20),
    .in21(registers32_1_outputr21), .in22(registers32_1_outputr22), .in23(registers32_1_outputr23),
    .in24(registers32_1_outputr24), .in25(registers32_1_outputr25), .in26(registers32_1_outputr26),
    .in27(registers32_1_outputr27), .in28(registers32_1_outputr28), .in29(registers32_1_outputr29),
    .in30(registers32_1_outputr30), .in31(registers32_1_outputr31), .out(READ2_OUTPUT), .sel(READ2_SELECT));
endmodule
